// Logisim project 18101269.circ as structural Verilog: 48 circuits, main circuit main
module main (
  input  Mode
);

  wire button_1_out, button_2_out, CLK_out, R0C0, R0C1, R0C2, R0C3, R0C4, R0C5, R1C0, R1C1, R1C2, R1C3, R1C4,
       R1C5, R2C0, R2C1, R2C2, R2C3, R2C4, R2C5, R3C0, R3C1, R3C2, R3C3, R3C4, R3C5, R4C0, R4C1, R4C2, R4C3,
       R4C4, R4C5, R5C0, R5C1, R5C2, R5C3, R5C4, R5C5;
  wire [3:0] n7_segment_display_1_p1, n7_segment_display_1_p2, n7_segment_display_3_p1,
       n7_segment_display_3_p2, viewer_1_cs10, viewer_1_ds10, viewer_1_s6, viewer_1_s10;
  wire [7:0] r0c0han_1_o0, r0c0han_1_o1, r0c0han_1_o2, r0c0han_1_o3, r0c0han_1_o4, r0c0han_1_o5,
       r0c0han_1_o6, r0c0han_1_o7, r0c1doo_1_o0, r0c1doo_1_o1, r0c1doo_1_o2, r0c1doo_1_o3, r0c1doo_1_o4,
       r0c1doo_1_o5, r0c1doo_1_o6, r0c1doo_1_o7, r0c2se_1_o0, r0c2se_1_o1, r0c2se_1_o2, r0c2se_1_o3,
       r0c2se_1_o4, r0c2se_1_o5, r0c2se_1_o6, r0c2se_1_o7, r0c3ne_1_o0, r0c3ne_1_o1, r0c3ne_1_o2,
       r0c3ne_1_o3, r0c3ne_1_o4, r0c3ne_1_o5, r0c3ne_1_o6, r0c3ne_1_o7, r0c4da_1_o0, r0c4da_1_o1,
       r0c4da_1_o2, r0c4da_1_o3, r0c4da_1_o4, r0c4da_1_o5, r0c4da_1_o6, r0c4da_1_o7, r0c5seoc_1_o0,
       r0c5seoc_1_o1, r0c5seoc_1_o2, r0c5seoc_1_o3, r0c5seoc_1_o4, r0c5seoc_1_o5, r0c5seoc_1_o6,
       r0c5seoc_1_o7, r1c0yu_1_o0, r1c0yu_1_o1, r1c0yu_1_o2, r1c0yu_1_o3, r1c0yu_1_o4, r1c0yu_1_o5,
       r1c0yu_1_o6, r1c0yu_1_o7, r1c1seoc_1_o0, r1c1seoc_1_o1, r1c1seoc_1_o2, r1c1seoc_1_o3, r1c1seoc_1_o4,
       r1c1seoc_1_o5, r1c1seoc_1_o6, r1c1seoc_1_o7, r1c2il_1_o0, r1c2il_1_o1, r1c2il_1_o2, r1c2il_1_o3,
       r1c2il_1_o4, r1c2il_1_o5, r1c2il_1_o6, r1c2il_1_o7, r1c3goq_1_o0, r1c3goq_1_o1, r1c3goq_1_o2,
       r1c3goq_1_o3, r1c3goq_1_o4, r1c3goq_1_o5, r1c3goq_1_o6, r1c3goq_1_o7, r1c4yu_1_o0, r1c4yu_1_o1,
       r1c4yu_1_o2, r1c4yu_1_o3, r1c4yu_1_o4, r1c4yu_1_o5, r1c4yu_1_o6, r1c4yu_1_o7, r1c5durb_1_o0,
       r1c5durb_1_o1, r1c5durb_1_o2, r1c5durb_1_o3, r1c5durb_1_o4, r1c5durb_1_o5, r1c5durb_1_o6,
       r1c5durb_1_o7, r2c0a_1_o0, r2c0a_1_o1, r2c0a_1_o2, r2c0a_1_o3, r2c0a_1_o4, r2c0a_1_o5, r2c0a_1_o6,
       r2c0a_1_o7, r2c1hop_1_o0, r2c1hop_1_o1, r2c1hop_1_o2, r2c1hop_1_o3, r2c1hop_1_o4, r2c1hop_1_o5,
       r2c1hop_1_o6, r2c1hop_1_o7, r2c2yul_1_o0, r2c2yul_1_o1, r2c2yul_1_o2, r2c2yul_1_o3, r2c2yul_1_o4,
       r2c2yul_1_o5, r2c2yul_1_o6, r2c2yul_1_o7, r2c3han_1_o0, r2c3han_1_o1, r2c3han_1_o2, r2c3han_1_o3,
       r2c3han_1_o4, r2c3han_1_o5, r2c3han_1_o6, r2c3han_1_o7, r2c4doo_1_o0, r2c4doo_1_o1, r2c4doo_1_o2,
       r2c4doo_1_o3, r2c4doo_1_o4, r2c4doo_1_o5, r2c4doo_1_o6, r2c4doo_1_o7, r2c5si_1_o0, r2c5si_1_o1,
       r2c5si_1_o2, r2c5si_1_o3, r2c5si_1_o4, r2c5si_1_o5, r2c5si_1_o6, r2c5si_1_o7, r3c0ja_1_o0,
       r3c0ja_1_o1, r3c0ja_1_o2, r3c0ja_1_o3, r3c0ja_1_o4, r3c0ja_1_o5, r3c0ja_1_o6, r3c0ja_1_o7,
       r3c1yi_1_o0, r3c1yi_1_o1, r3c1yi_1_o2, r3c1yi_1_o3, r3c1yi_1_o4, r3c1yi_1_o5, r3c1yi_1_o6,
       r3c1yi_1_o7, r3c2sam_1_o0, r3c2sam_1_o1, r3c2sam_1_o2, r3c2sam_1_o3, r3c2sam_1_o4, r3c2sam_1_o5,
       r3c2sam_1_o6, r3c2sam_1_o7, r3c3sa_1_o0, r3c3sa_1_o1, r3c3sa_1_o2, r3c3sa_1_o3, r3c3sa_1_o4,
       r3c3sa_1_o5, r3c3sa_1_o6, r3c3sa_1_o7, r3c4o_1_o0, r3c4o_1_o1, r3c4o_1_o2, r3c4o_1_o3, r3c4o_1_o4,
       r3c4o_1_o5, r3c4o_1_o6, r3c4o_1_o7, r3c5siq_1_o0, r3c5siq_1_o1, r3c5siq_1_o2, r3c5siq_1_o3,
       r3c5siq_1_o4, r3c5siq_1_o5, r3c5siq_1_o6, r3c5siq_1_o7, r4c0jeong_1_o0, r4c0jeong_1_o1,
       r4c0jeong_1_o2, r4c0jeong_1_o3, r4c0jeong_1_o4, r4c0jeong_1_o5, r4c0jeong_1_o6, r4c0jeong_1_o7,
       r4c1il_1_o0, r4c1il_1_o1, r4c1il_1_o2, r4c1il_1_o3, r4c1il_1_o4, r4c1il_1_o5, r4c1il_1_o6,
       r4c1il_1_o7, r4c2yi_1_o0, r4c2yi_1_o1, r4c2yi_1_o2, r4c2yi_1_o3, r4c2yi_1_o4, r4c2yi_1_o5,
       r4c2yi_1_o6, r4c2yi_1_o7, r4c3sam_1_o0, r4c3sam_1_o1, r4c3sam_1_o2, r4c3sam_1_o3, r4c3sam_1_o4,
       r4c3sam_1_o5, r4c3sam_1_o6, r4c3sam_1_o7, r4c4sa_1_o0, r4c4sa_1_o1, r4c4sa_1_o2, r4c4sa_1_o3,
       r4c4sa_1_o4, r4c4sa_1_o5, r4c4sa_1_o6, r4c4sa_1_o7, r4c5yuk_1_o0, r4c5yuk_1_o1, r4c5yuk_1_o2,
       r4c5yuk_1_o3, r4c5yuk_1_o4, r4c5yuk_1_o5, r4c5yuk_1_o6, r4c5yuk_1_o7, r5c0o_1_o0, r5c0o_1_o1,
       r5c0o_1_o2, r5c0o_1_o3, r5c0o_1_o4, r5c0o_1_o5, r5c0o_1_o6, r5c0o_1_o7, r5c1o_1_o0, r5c1o_1_o1,
       r5c1o_1_o2, r5c1o_1_o3, r5c1o_1_o4, r5c1o_1_o5, r5c1o_1_o6, r5c1o_1_o7, r5c2chil_1_o0, r5c2chil_1_o1,
       r5c2chil_1_o2, r5c2chil_1_o3, r5c2chil_1_o4, r5c2chil_1_o5, r5c2chil_1_o6, r5c2chil_1_o7,
       r5c3pal_1_o0, r5c3pal_1_o1, r5c3pal_1_o2, r5c3pal_1_o3, r5c3pal_1_o4, r5c3pal_1_o5, r5c3pal_1_o6,
       r5c3pal_1_o7, r5c4koo_1_o0, r5c4koo_1_o1, r5c4koo_1_o2, r5c4koo_1_o3, r5c4koo_1_o4, r5c4koo_1_o5,
       r5c4koo_1_o6, r5c4koo_1_o7, r5c5boon_1_o0, r5c5boon_1_o1, r5c5boon_1_o2, r5c5boon_1_o3, r5c5boon_1_o4,
       r5c5boon_1_o5, r5c5boon_1_o6, r5c5boon_1_o7;

  Clock CLK (.out(CLK_out));
  // _7_Segment_Display 7_segment_display_1: pin names not known; wires that end beside it: n7_segment_display_1_p1, n7_segment_display_1_p2
  // BCD_to_7_Segment_decoder bcd_to_7_segment_decoder_1: pin names not known
  _7_Segment_Display u_7_segment_display_2 ();  // open: g, f, a, b, e, d, c, dp
  // _7_Segment_Display 7_segment_display_3: pin names not known; wires that end beside it: n7_segment_display_3_p1, n7_segment_display_3_p2
  // BCD_to_7_Segment_decoder bcd_to_7_segment_decoder_2: pin names not known
  // BCD_to_7_Segment_decoder bcd_to_7_segment_decoder_3: pin names not known
  Button button_1 (.out(button_1_out));
  _7_Segment_Display u_7_segment_display_4 ();  // open: g, f, a, b, e, d, c, dp
  // BCD_to_7_Segment_decoder bcd_to_7_segment_decoder_4: pin names not known
  Viewer viewer_1 (
    .Mode(Mode), .CLK(CLK_out), .MinSet(button_2_out), .HourSet(button_1_out), .R0C0(R0C0), .R0C1(R0C1),
    .R0C2(R0C2), .R0C3(R0C3), .R0C4(R0C4), .R0C5(R0C5), .R1C0(R1C0), .R1C1(R1C1), .R1C2(R1C2), .R1C3(R1C3),
    .R1C4(R1C4), .R1C5(R1C5), .R2C0(R2C0), .R2C1(R2C1), .R2C2(R2C2), .R2C3(R2C3), .R2C4(R2C4), .R2C5(R2C5),
    .R3C0(R3C0), .R3C1(R3C1), .R3C2(R3C2), .R3C3(R3C3), .R3C4(R3C4), .R3C5(R3C5), .R4C0(R4C0), .R4C1(R4C1),
    .R4C2(R4C2), .R4C3(R4C3), .R4C4(R4C4), .R4C5(R4C5), .R5C0(R5C0), .R5C1(R5C1), .R5C2(R5C2), .R5C3(R5C3),
    .R5C4(R5C4), .R5C5(R5C5), .S10(viewer_1_s10), .S6(viewer_1_s6), .M10(n7_segment_display_3_p2),
    .M6(n7_segment_display_3_p1), .H2(n7_segment_display_1_p2), .H10(n7_segment_display_1_p1),
    .CS10(viewer_1_cs10), .DS10(viewer_1_ds10));
  // _7_Segment_Display 7_segment_display_5: pin names not known; wires that end beside it: viewer_1_s6, viewer_1_s10
  _7_Segment_Display u_7_segment_display_6 ();  // open: g, f, a, b, e, d, c, dp
  // BCD_to_7_Segment_decoder bcd_to_7_segment_decoder_5: pin names not known
  // BCD_to_7_Segment_decoder bcd_to_7_segment_decoder_6: pin names not known
  Button button_2 (.out(button_2_out));
  // _7_Segment_Display 7_segment_display_7: pin names not known; wires that end beside it: viewer_1_ds10, viewer_1_cs10
  // BCD_to_7_Segment_decoder bcd_to_7_segment_decoder_7: pin names not known
  _7_Segment_Display u_7_segment_display_8 ();  // open: g, f, a, b, e, d, c, dp
  // BCD_to_7_Segment_decoder bcd_to_7_segment_decoder_8: pin names not known
  DotMatrix #(.dotshape("circle"), .matrixcols(8), .matrixrows(8)) dotmatrix_1 (
    .col0(r0c0han_1_o0), .col1(r0c0han_1_o1), .col2(r0c0han_1_o2), .col3(r0c0han_1_o3), .col4(r0c0han_1_o4),
    .col5(r0c0han_1_o5), .col6(r0c0han_1_o6), .col7(r0c0han_1_o7));
  R0C0Han r0c0han_1 (
    .E(R0C0), .O0(r0c0han_1_o0), .O1(r0c0han_1_o1), .O2(r0c0han_1_o2), .O3(r0c0han_1_o3), .O4(r0c0han_1_o4),
    .O5(r0c0han_1_o5), .O6(r0c0han_1_o6), .O7(r0c0han_1_o7));
  DotMatrix #(.dotshape("circle"), .matrixcols(8), .matrixrows(8)) dotmatrix_2 (
    .col0(r1c0yu_1_o0), .col1(r1c0yu_1_o1), .col2(r1c0yu_1_o2), .col3(r1c0yu_1_o3), .col4(r1c0yu_1_o4),
    .col5(r1c0yu_1_o5), .col6(r1c0yu_1_o6), .col7(r1c0yu_1_o7));
  R1C0Yu r1c0yu_1 (
    .E(R1C0), .O0(r1c0yu_1_o0), .O1(r1c0yu_1_o1), .O2(r1c0yu_1_o2), .O3(r1c0yu_1_o3), .O4(r1c0yu_1_o4),
    .O5(r1c0yu_1_o5), .O6(r1c0yu_1_o6), .O7(r1c0yu_1_o7));
  DotMatrix #(.dotshape("circle"), .matrixcols(8), .matrixrows(8)) dotmatrix_3 (
    .col0(r2c0a_1_o0), .col1(r2c0a_1_o1), .col2(r2c0a_1_o2), .col3(r2c0a_1_o3), .col4(r2c0a_1_o4),
    .col5(r2c0a_1_o5), .col6(r2c0a_1_o6), .col7(r2c0a_1_o7));
  R2C0A r2c0a_1 (
    .E(R2C0), .O0(r2c0a_1_o0), .O1(r2c0a_1_o1), .O2(r2c0a_1_o2), .O3(r2c0a_1_o3), .O4(r2c0a_1_o4),
    .O5(r2c0a_1_o5), .O6(r2c0a_1_o6), .O7(r2c0a_1_o7));
  DotMatrix #(.dotshape("circle"), .matrixcols(8), .matrixrows(8)) dotmatrix_4 (
    .col0(r3c0ja_1_o0), .col1(r3c0ja_1_o1), .col2(r3c0ja_1_o2), .col3(r3c0ja_1_o3), .col4(r3c0ja_1_o4),
    .col5(r3c0ja_1_o5), .col6(r3c0ja_1_o6), .col7(r3c0ja_1_o7));
  R3C0Ja r3c0ja_1 (
    .E(R3C0), .O0(r3c0ja_1_o0), .O1(r3c0ja_1_o1), .O2(r3c0ja_1_o2), .O3(r3c0ja_1_o3), .O4(r3c0ja_1_o4),
    .O5(r3c0ja_1_o5), .O6(r3c0ja_1_o6), .O7(r3c0ja_1_o7));
  DotMatrix #(.dotshape("circle"), .matrixcols(8), .matrixrows(8)) dotmatrix_5 (
    .col0(r4c0jeong_1_o0), .col1(r4c0jeong_1_o1), .col2(r4c0jeong_1_o2), .col3(r4c0jeong_1_o3),
    .col4(r4c0jeong_1_o4), .col5(r4c0jeong_1_o5), .col6(r4c0jeong_1_o6), .col7(r4c0jeong_1_o7));
  R4C0Jeong r4c0jeong_1 (
    .E(R4C0), .O0(r4c0jeong_1_o0), .O1(r4c0jeong_1_o1), .O2(r4c0jeong_1_o2), .O3(r4c0jeong_1_o3),
    .O4(r4c0jeong_1_o4), .O5(r4c0jeong_1_o5), .O6(r4c0jeong_1_o6), .O7(r4c0jeong_1_o7));
  DotMatrix #(.dotshape("circle"), .matrixcols(8), .matrixrows(8)) dotmatrix_6 (
    .col0(r5c0o_1_o0), .col1(r5c0o_1_o1), .col2(r5c0o_1_o2), .col3(r5c0o_1_o3), .col4(r5c0o_1_o4),
    .col5(r5c0o_1_o5), .col6(r5c0o_1_o6), .col7(r5c0o_1_o7));
  R5C0O r5c0o_1 (
    .E(R5C0), .O0(r5c0o_1_o0), .O1(r5c0o_1_o1), .O2(r5c0o_1_o2), .O3(r5c0o_1_o3), .O4(r5c0o_1_o4),
    .O5(r5c0o_1_o5), .O6(r5c0o_1_o6), .O7(r5c0o_1_o7));
  DotMatrix #(.dotshape("circle"), .matrixcols(8), .matrixrows(8)) dotmatrix_7 (
    .col0(r0c1doo_1_o0), .col1(r0c1doo_1_o1), .col2(r0c1doo_1_o2), .col3(r0c1doo_1_o3), .col4(r0c1doo_1_o4),
    .col5(r0c1doo_1_o5), .col6(r0c1doo_1_o6), .col7(r0c1doo_1_o7));
  R0C1Doo r0c1doo_1 (
    .E(R0C1), .O0(r0c1doo_1_o0), .O1(r0c1doo_1_o1), .O2(r0c1doo_1_o2), .O3(r0c1doo_1_o3), .O4(r0c1doo_1_o4),
    .O5(r0c1doo_1_o5), .O6(r0c1doo_1_o6), .O7(r0c1doo_1_o7));
  DotMatrix #(.dotshape("circle"), .matrixcols(8), .matrixrows(8)) dotmatrix_8 (
    .col0(r1c1seoc_1_o0), .col1(r1c1seoc_1_o1), .col2(r1c1seoc_1_o2), .col3(r1c1seoc_1_o3),
    .col4(r1c1seoc_1_o4), .col5(r1c1seoc_1_o5), .col6(r1c1seoc_1_o6), .col7(r1c1seoc_1_o7));
  R1C1Seoc r1c1seoc_1 (
    .E(R1C1), .O0(r1c1seoc_1_o0), .O1(r1c1seoc_1_o1), .O2(r1c1seoc_1_o2), .O3(r1c1seoc_1_o3),
    .O4(r1c1seoc_1_o4), .O5(r1c1seoc_1_o5), .O6(r1c1seoc_1_o6), .O7(r1c1seoc_1_o7));
  DotMatrix #(.dotshape("circle"), .matrixcols(8), .matrixrows(8)) dotmatrix_9 (
    .col0(r2c1hop_1_o0), .col1(r2c1hop_1_o1), .col2(r2c1hop_1_o2), .col3(r2c1hop_1_o3), .col4(r2c1hop_1_o4),
    .col5(r2c1hop_1_o5), .col6(r2c1hop_1_o6), .col7(r2c1hop_1_o7));
  R2C1Hop r2c1hop_1 (
    .E(R2C1), .O0(r2c1hop_1_o0), .O1(r2c1hop_1_o1), .O2(r2c1hop_1_o2), .O3(r2c1hop_1_o3), .O4(r2c1hop_1_o4),
    .O5(r2c1hop_1_o5), .O6(r2c1hop_1_o6), .O7(r2c1hop_1_o7));
  DotMatrix #(.dotshape("circle"), .matrixcols(8), .matrixrows(8)) dotmatrix_10 (
    .col0(r3c1yi_1_o0), .col1(r3c1yi_1_o1), .col2(r3c1yi_1_o2), .col3(r3c1yi_1_o3), .col4(r3c1yi_1_o4),
    .col5(r3c1yi_1_o5), .col6(r3c1yi_1_o6), .col7(r3c1yi_1_o7));
  R3C1Yi r3c1yi_1 (
    .E(R3C1), .O0(r3c1yi_1_o0), .O1(r3c1yi_1_o1), .O2(r3c1yi_1_o2), .O3(r3c1yi_1_o3), .O4(r3c1yi_1_o4),
    .O5(r3c1yi_1_o5), .O6(r3c1yi_1_o6), .O7(r3c1yi_1_o7));
  DotMatrix #(.dotshape("circle"), .matrixcols(8), .matrixrows(8)) dotmatrix_11 (
    .col0(r4c1il_1_o0), .col1(r4c1il_1_o1), .col2(r4c1il_1_o2), .col3(r4c1il_1_o3), .col4(r4c1il_1_o4),
    .col5(r4c1il_1_o5), .col6(r4c1il_1_o6), .col7(r4c1il_1_o7));
  R4C1Il r4c1il_1 (
    .E(R4C1), .O0(r4c1il_1_o0), .O1(r4c1il_1_o1), .O2(r4c1il_1_o2), .O3(r4c1il_1_o3), .O4(r4c1il_1_o4),
    .O5(r4c1il_1_o5), .O6(r4c1il_1_o6), .O7(r4c1il_1_o7));
  DotMatrix #(.dotshape("circle"), .matrixcols(8), .matrixrows(8)) dotmatrix_12 (
    .col0(r5c1o_1_o0), .col1(r5c1o_1_o1), .col2(r5c1o_1_o2), .col3(r5c1o_1_o3), .col4(r5c1o_1_o4),
    .col5(r5c1o_1_o5), .col6(r5c1o_1_o6), .col7(r5c1o_1_o7));
  R5C1O r5c1o_1 (
    .E(R5C1), .O0(r5c1o_1_o0), .O1(r5c1o_1_o1), .O2(r5c1o_1_o2), .O3(r5c1o_1_o3), .O4(r5c1o_1_o4),
    .O5(r5c1o_1_o5), .O6(r5c1o_1_o6), .O7(r5c1o_1_o7));
  R0C2Se r0c2se_1 (
    .E(R0C2), .O0(r0c2se_1_o0), .O1(r0c2se_1_o1), .O2(r0c2se_1_o2), .O3(r0c2se_1_o3), .O4(r0c2se_1_o4),
    .O5(r0c2se_1_o5), .O6(r0c2se_1_o6), .O7(r0c2se_1_o7));
  R1C2Il r1c2il_1 (
    .E(R1C2), .O0(r1c2il_1_o0), .O1(r1c2il_1_o1), .O2(r1c2il_1_o2), .O3(r1c2il_1_o3), .O4(r1c2il_1_o4),
    .O5(r1c2il_1_o5), .O6(r1c2il_1_o6), .O7(r1c2il_1_o7));
  R2C2Yul r2c2yul_1 (
    .E(R2C2), .O0(r2c2yul_1_o0), .O1(r2c2yul_1_o1), .O2(r2c2yul_1_o2), .O3(r2c2yul_1_o3), .O4(r2c2yul_1_o4),
    .O5(r2c2yul_1_o5), .O6(r2c2yul_1_o6), .O7(r2c2yul_1_o7));
  R3C2Sam r3c2sam_1 (
    .E(R3C2), .O0(r3c2sam_1_o0), .O1(r3c2sam_1_o1), .O2(r3c2sam_1_o2), .O3(r3c2sam_1_o3), .O4(r3c2sam_1_o4),
    .O5(r3c2sam_1_o5), .O6(r3c2sam_1_o6), .O7(r3c2sam_1_o7));
  R4C2Yi r4c2yi_1 (
    .E(R4C2), .O0(r4c2yi_1_o0), .O1(r4c2yi_1_o1), .O2(r4c2yi_1_o2), .O3(r4c2yi_1_o3), .O4(r4c2yi_1_o4),
    .O5(r4c2yi_1_o5), .O6(r4c2yi_1_o6), .O7(r4c2yi_1_o7));
  R5C2Chil r5c2chil_1 (
    .E(R5C2), .O0(r5c2chil_1_o0), .O1(r5c2chil_1_o1), .O2(r5c2chil_1_o2), .O3(r5c2chil_1_o3),
    .O4(r5c2chil_1_o4), .O5(r5c2chil_1_o5), .O6(r5c2chil_1_o6), .O7(r5c2chil_1_o7));
  DotMatrix #(.dotshape("circle"), .matrixcols(8), .matrixrows(8)) dotmatrix_13 (
    .col0(r0c2se_1_o0), .col1(r0c2se_1_o1), .col2(r0c2se_1_o2), .col3(r0c2se_1_o3), .col4(r0c2se_1_o4),
    .col5(r0c2se_1_o5), .col6(r0c2se_1_o6), .col7(r0c2se_1_o7));
  DotMatrix #(.dotshape("circle"), .matrixcols(8), .matrixrows(8)) dotmatrix_14 (
    .col0(r1c2il_1_o0), .col1(r1c2il_1_o1), .col2(r1c2il_1_o2), .col3(r1c2il_1_o3), .col4(r1c2il_1_o4),
    .col5(r1c2il_1_o5), .col6(r1c2il_1_o6), .col7(r1c2il_1_o7));
  DotMatrix #(.dotshape("circle"), .matrixcols(8), .matrixrows(8)) dotmatrix_15 (
    .col0(r2c2yul_1_o0), .col1(r2c2yul_1_o1), .col2(r2c2yul_1_o2), .col3(r2c2yul_1_o3), .col4(r2c2yul_1_o4),
    .col5(r2c2yul_1_o5), .col6(r2c2yul_1_o6), .col7(r2c2yul_1_o7));
  DotMatrix #(.dotshape("circle"), .matrixcols(8), .matrixrows(8)) dotmatrix_16 (
    .col0(r3c2sam_1_o0), .col1(r3c2sam_1_o1), .col2(r3c2sam_1_o2), .col3(r3c2sam_1_o3), .col4(r3c2sam_1_o4),
    .col5(r3c2sam_1_o5), .col6(r3c2sam_1_o6), .col7(r3c2sam_1_o7));
  DotMatrix #(.dotshape("circle"), .matrixcols(8), .matrixrows(8)) dotmatrix_17 (
    .col0(r4c2yi_1_o0), .col1(r4c2yi_1_o1), .col2(r4c2yi_1_o2), .col3(r4c2yi_1_o3), .col4(r4c2yi_1_o4),
    .col5(r4c2yi_1_o5), .col6(r4c2yi_1_o6), .col7(r4c2yi_1_o7));
  DotMatrix #(.dotshape("circle"), .matrixcols(8), .matrixrows(8)) dotmatrix_18 (
    .col0(r5c2chil_1_o0), .col1(r5c2chil_1_o1), .col2(r5c2chil_1_o2), .col3(r5c2chil_1_o3),
    .col4(r5c2chil_1_o4), .col5(r5c2chil_1_o5), .col6(r5c2chil_1_o6), .col7(r5c2chil_1_o7));
  R0C3Ne r0c3ne_1 (
    .E(R0C3), .O0(r0c3ne_1_o0), .O1(r0c3ne_1_o1), .O2(r0c3ne_1_o2), .O3(r0c3ne_1_o3), .O4(r0c3ne_1_o4),
    .O5(r0c3ne_1_o5), .O6(r0c3ne_1_o6), .O7(r0c3ne_1_o7));
  R1C3Goq r1c3goq_1 (
    .E(R1C3), .O0(r1c3goq_1_o0), .O1(r1c3goq_1_o1), .O2(r1c3goq_1_o2), .O3(r1c3goq_1_o3), .O4(r1c3goq_1_o4),
    .O5(r1c3goq_1_o5), .O6(r1c3goq_1_o6), .O7(r1c3goq_1_o7));
  R2C3Han r2c3han_1 (
    .E(R2C3), .O0(r2c3han_1_o0), .O1(r2c3han_1_o1), .O2(r2c3han_1_o2), .O3(r2c3han_1_o3), .O4(r2c3han_1_o4),
    .O5(r2c3han_1_o5), .O6(r2c3han_1_o6), .O7(r2c3han_1_o7));
  R3C3Sa r3c3sa_1 (
    .E(R3C3), .O0(r3c3sa_1_o0), .O1(r3c3sa_1_o1), .O2(r3c3sa_1_o2), .O3(r3c3sa_1_o3), .O4(r3c3sa_1_o4),
    .O5(r3c3sa_1_o5), .O6(r3c3sa_1_o6), .O7(r3c3sa_1_o7));
  R4C3Sam r4c3sam_1 (
    .E(R4C3), .O0(r4c3sam_1_o0), .O1(r4c3sam_1_o1), .O2(r4c3sam_1_o2), .O3(r4c3sam_1_o3), .O4(r4c3sam_1_o4),
    .O5(r4c3sam_1_o5), .O6(r4c3sam_1_o6), .O7(r4c3sam_1_o7));
  R5C3Pal r5c3pal_1 (
    .E(R5C3), .O0(r5c3pal_1_o0), .O1(r5c3pal_1_o1), .O2(r5c3pal_1_o2), .O3(r5c3pal_1_o3), .O4(r5c3pal_1_o4),
    .O5(r5c3pal_1_o5), .O6(r5c3pal_1_o6), .O7(r5c3pal_1_o7));
  DotMatrix #(.dotshape("circle"), .matrixcols(8), .matrixrows(8)) dotmatrix_19 (
    .col0(r0c3ne_1_o0), .col1(r0c3ne_1_o1), .col2(r0c3ne_1_o2), .col3(r0c3ne_1_o3), .col4(r0c3ne_1_o4),
    .col5(r0c3ne_1_o5), .col6(r0c3ne_1_o6), .col7(r0c3ne_1_o7));
  DotMatrix #(.dotshape("circle"), .matrixcols(8), .matrixrows(8)) dotmatrix_20 (
    .col0(r1c3goq_1_o0), .col1(r1c3goq_1_o1), .col2(r1c3goq_1_o2), .col3(r1c3goq_1_o3), .col4(r1c3goq_1_o4),
    .col5(r1c3goq_1_o5), .col6(r1c3goq_1_o6), .col7(r1c3goq_1_o7));
  DotMatrix #(.dotshape("circle"), .matrixcols(8), .matrixrows(8)) dotmatrix_21 (
    .col0(r2c3han_1_o0), .col1(r2c3han_1_o1), .col2(r2c3han_1_o2), .col3(r2c3han_1_o3), .col4(r2c3han_1_o4),
    .col5(r2c3han_1_o5), .col6(r2c3han_1_o6), .col7(r2c3han_1_o7));
  DotMatrix #(.dotshape("circle"), .matrixcols(8), .matrixrows(8)) dotmatrix_22 (
    .col0(r3c3sa_1_o0), .col1(r3c3sa_1_o1), .col2(r3c3sa_1_o2), .col3(r3c3sa_1_o3), .col4(r3c3sa_1_o4),
    .col5(r3c3sa_1_o5), .col6(r3c3sa_1_o6), .col7(r3c3sa_1_o7));
  DotMatrix #(.dotshape("circle"), .matrixcols(8), .matrixrows(8)) dotmatrix_23 (
    .col0(r4c3sam_1_o0), .col1(r4c3sam_1_o1), .col2(r4c3sam_1_o2), .col3(r4c3sam_1_o3), .col4(r4c3sam_1_o4),
    .col5(r4c3sam_1_o5), .col6(r4c3sam_1_o6), .col7(r4c3sam_1_o7));
  DotMatrix #(.dotshape("circle"), .matrixcols(8), .matrixrows(8)) dotmatrix_24 (
    .col0(r5c3pal_1_o0), .col1(r5c3pal_1_o1), .col2(r5c3pal_1_o2), .col3(r5c3pal_1_o3), .col4(r5c3pal_1_o4),
    .col5(r5c3pal_1_o5), .col6(r5c3pal_1_o6), .col7(r5c3pal_1_o7));
  DotMatrix #(.dotshape("circle"), .matrixcols(8), .matrixrows(8)) dotmatrix_25 (
    .col0(r0c4da_1_o0), .col1(r0c4da_1_o1), .col2(r0c4da_1_o2), .col3(r0c4da_1_o3), .col4(r0c4da_1_o4),
    .col5(r0c4da_1_o5), .col6(r0c4da_1_o6), .col7(r0c4da_1_o7));
  R0C4Da r0c4da_1 (
    .E(R0C4), .O0(r0c4da_1_o0), .O1(r0c4da_1_o1), .O2(r0c4da_1_o2), .O3(r0c4da_1_o3), .O4(r0c4da_1_o4),
    .O5(r0c4da_1_o5), .O6(r0c4da_1_o6), .O7(r0c4da_1_o7));
  DotMatrix #(.dotshape("circle"), .matrixcols(8), .matrixrows(8)) dotmatrix_26 (
    .col0(r1c4yu_1_o0), .col1(r1c4yu_1_o1), .col2(r1c4yu_1_o2), .col3(r1c4yu_1_o3), .col4(r1c4yu_1_o4),
    .col5(r1c4yu_1_o5), .col6(r1c4yu_1_o6), .col7(r1c4yu_1_o7));
  R1C4Yu r1c4yu_1 (
    .E(R1C4), .O0(r1c4yu_1_o0), .O1(r1c4yu_1_o1), .O2(r1c4yu_1_o2), .O3(r1c4yu_1_o3), .O4(r1c4yu_1_o4),
    .O5(r1c4yu_1_o5), .O6(r1c4yu_1_o6), .O7(r1c4yu_1_o7));
  DotMatrix #(.dotshape("circle"), .matrixcols(8), .matrixrows(8)) dotmatrix_27 (
    .col0(r2c4doo_1_o0), .col1(r2c4doo_1_o1), .col2(r2c4doo_1_o2), .col3(r2c4doo_1_o3), .col4(r2c4doo_1_o4),
    .col5(r2c4doo_1_o5), .col6(r2c4doo_1_o6), .col7(r2c4doo_1_o7));
  R2C4Doo r2c4doo_1 (
    .E(R2C4), .O0(r2c4doo_1_o0), .O1(r2c4doo_1_o1), .O2(r2c4doo_1_o2), .O3(r2c4doo_1_o3), .O4(r2c4doo_1_o4),
    .O5(r2c4doo_1_o5), .O6(r2c4doo_1_o6), .O7(r2c4doo_1_o7));
  DotMatrix #(.dotshape("circle"), .matrixcols(8), .matrixrows(8)) dotmatrix_28 (
    .col0(r3c4o_1_o0), .col1(r3c4o_1_o1), .col2(r3c4o_1_o2), .col3(r3c4o_1_o3), .col4(r3c4o_1_o4),
    .col5(r3c4o_1_o5), .col6(r3c4o_1_o6), .col7(r3c4o_1_o7));
  R3C4O r3c4o_1 (
    .E(R3C4), .O0(r3c4o_1_o0), .O1(r3c4o_1_o1), .O2(r3c4o_1_o2), .O3(r3c4o_1_o3), .O4(r3c4o_1_o4),
    .O5(r3c4o_1_o5), .O6(r3c4o_1_o6), .O7(r3c4o_1_o7));
  DotMatrix #(.dotshape("circle"), .matrixcols(8), .matrixrows(8)) dotmatrix_29 (
    .col0(r4c4sa_1_o0), .col1(r4c4sa_1_o1), .col2(r4c4sa_1_o2), .col3(r4c4sa_1_o3), .col4(r4c4sa_1_o4),
    .col5(r4c4sa_1_o5), .col6(r4c4sa_1_o6), .col7(r4c4sa_1_o7));
  R4C4Sa r4c4sa_1 (
    .E(R4C4), .O0(r4c4sa_1_o0), .O1(r4c4sa_1_o1), .O2(r4c4sa_1_o2), .O3(r4c4sa_1_o3), .O4(r4c4sa_1_o4),
    .O5(r4c4sa_1_o5), .O6(r4c4sa_1_o6), .O7(r4c4sa_1_o7));
  DotMatrix #(.dotshape("circle"), .matrixcols(8), .matrixrows(8)) dotmatrix_30 (
    .col0(r5c4koo_1_o0), .col1(r5c4koo_1_o1), .col2(r5c4koo_1_o2), .col3(r5c4koo_1_o3), .col4(r5c4koo_1_o4),
    .col5(r5c4koo_1_o5), .col6(r5c4koo_1_o6), .col7(r5c4koo_1_o7));
  R5C4Koo r5c4koo_1 (
    .E(R5C4), .O0(r5c4koo_1_o0), .O1(r5c4koo_1_o1), .O2(r5c4koo_1_o2), .O3(r5c4koo_1_o3), .O4(r5c4koo_1_o4),
    .O5(r5c4koo_1_o5), .O6(r5c4koo_1_o6), .O7(r5c4koo_1_o7));
  DotMatrix #(.dotshape("circle"), .matrixcols(8), .matrixrows(8)) dotmatrix_31 (
    .col0(r0c5seoc_1_o0), .col1(r0c5seoc_1_o1), .col2(r0c5seoc_1_o2), .col3(r0c5seoc_1_o3),
    .col4(r0c5seoc_1_o4), .col5(r0c5seoc_1_o5), .col6(r0c5seoc_1_o6), .col7(r0c5seoc_1_o7));
  R0C5Seoc r0c5seoc_1 (
    .E(R0C5), .O0(r0c5seoc_1_o0), .O1(r0c5seoc_1_o1), .O2(r0c5seoc_1_o2), .O3(r0c5seoc_1_o3),
    .O4(r0c5seoc_1_o4), .O5(r0c5seoc_1_o5), .O6(r0c5seoc_1_o6), .O7(r0c5seoc_1_o7));
  DotMatrix #(.dotshape("circle"), .matrixcols(8), .matrixrows(8)) dotmatrix_32 (
    .col0(r1c5durb_1_o0), .col1(r1c5durb_1_o1), .col2(r1c5durb_1_o2), .col3(r1c5durb_1_o3),
    .col4(r1c5durb_1_o4), .col5(r1c5durb_1_o5), .col6(r1c5durb_1_o6), .col7(r1c5durb_1_o7));
  R1C5Durb r1c5durb_1 (
    .E(R1C5), .O0(r1c5durb_1_o0), .O1(r1c5durb_1_o1), .O2(r1c5durb_1_o2), .O3(r1c5durb_1_o3),
    .O4(r1c5durb_1_o4), .O5(r1c5durb_1_o5), .O6(r1c5durb_1_o6), .O7(r1c5durb_1_o7));
  DotMatrix #(.dotshape("circle"), .matrixcols(8), .matrixrows(8)) dotmatrix_33 (
    .col0(r2c5si_1_o0), .col1(r2c5si_1_o1), .col2(r2c5si_1_o2), .col3(r2c5si_1_o3), .col4(r2c5si_1_o4),
    .col5(r2c5si_1_o5), .col6(r2c5si_1_o6), .col7(r2c5si_1_o7));
  R2C5Si r2c5si_1 (
    .E(R2C5), .O0(r2c5si_1_o0), .O1(r2c5si_1_o1), .O2(r2c5si_1_o2), .O3(r2c5si_1_o3), .O4(r2c5si_1_o4),
    .O5(r2c5si_1_o5), .O6(r2c5si_1_o6), .O7(r2c5si_1_o7));
  DotMatrix #(.dotshape("circle"), .matrixcols(8), .matrixrows(8)) dotmatrix_34 (
    .col0(r3c5siq_1_o0), .col1(r3c5siq_1_o1), .col2(r3c5siq_1_o2), .col3(r3c5siq_1_o3), .col4(r3c5siq_1_o4),
    .col5(r3c5siq_1_o5), .col6(r3c5siq_1_o6), .col7(r3c5siq_1_o7));
  R3C5Siq r3c5siq_1 (
    .E(R3C5), .O0(r3c5siq_1_o0), .O1(r3c5siq_1_o1), .O2(r3c5siq_1_o2), .O3(r3c5siq_1_o3), .O4(r3c5siq_1_o4),
    .O5(r3c5siq_1_o5), .O6(r3c5siq_1_o6), .O7(r3c5siq_1_o7));
  DotMatrix #(.dotshape("circle"), .matrixcols(8), .matrixrows(8)) dotmatrix_35 (
    .col0(r4c5yuk_1_o0), .col1(r4c5yuk_1_o1), .col2(r4c5yuk_1_o2), .col3(r4c5yuk_1_o3), .col4(r4c5yuk_1_o4),
    .col5(r4c5yuk_1_o5), .col6(r4c5yuk_1_o6), .col7(r4c5yuk_1_o7));
  R4C5Yuk r4c5yuk_1 (
    .E(R4C5), .O0(r4c5yuk_1_o0), .O1(r4c5yuk_1_o1), .O2(r4c5yuk_1_o2), .O3(r4c5yuk_1_o3), .O4(r4c5yuk_1_o4),
    .O5(r4c5yuk_1_o5), .O6(r4c5yuk_1_o6), .O7(r4c5yuk_1_o7));
  DotMatrix #(.dotshape("circle"), .matrixcols(8), .matrixrows(8)) dotmatrix_36 (
    .col0(r5c5boon_1_o0), .col1(r5c5boon_1_o1), .col2(r5c5boon_1_o2), .col3(r5c5boon_1_o3),
    .col4(r5c5boon_1_o4), .col5(r5c5boon_1_o5), .col6(r5c5boon_1_o6), .col7(r5c5boon_1_o7));
  R5C5Boon r5c5boon_1 (
    .E(R5C5), .O0(r5c5boon_1_o0), .O1(r5c5boon_1_o1), .O2(r5c5boon_1_o2), .O3(r5c5boon_1_o3),
    .O4(r5c5boon_1_o4), .O5(r5c5boon_1_o5), .O6(r5c5boon_1_o6), .O7(r5c5boon_1_o7));

  // Notes on the sheet:
  //   Mode: 0=time set, 1=run
  //   시
  //   분
  //   18101269 정동하
  //   초
  //   1. Mode를 1로 설정해주세요.
  //   3. 비율은 0.45배를 추천드립니다.
  //   2. logisim 상단 Simulate 에서 Auto-Tick Enabled를 설정해주세요.
  //   1. Mode를 1로 설정해주세요.
  //   3. 비율은 0.45배를 추천드립니다.
  //   2. logisim 상단 Simulate 에서 Auto-Tick Enabled를 설정해주세요.
endmodule

module Counter6 (
  input  CLK,
  input  EI,
  output [2:0] O,
  output EO
);

  wire counter_1_carry;

  Counter #(.max('h5), .width(3)) counter_1 (
    .count(EI), .Q(O), .carry(counter_1_carry), .clk(CLK));  // open: load, D, up, clr
  and and_1 (EO, counter_1_carry, EI);
endmodule

module Counter10 (
  input  CLK,
  input  EI,
  output [3:0] O,
  output EO
);

  wire counter_1_carry;

  Counter #(.max('h9), .width(4)) counter_1 (
    .count(EI), .Q(O), .carry(counter_1_carry), .clk(CLK));  // open: load, D, up, clr
  and and_1 (EO, counter_1_carry, EI);
endmodule

module Counter12 (
  input  CLK,
  input  EI,
  output [3:0] O,
  output EO
);

  wire counter_1_carry;

  Counter #(.max('hb), .width(4)) counter_1 (
    .count(EI), .Q(O), .carry(counter_1_carry), .clk(CLK));  // open: load, D, up, clr
  and and_1 (EO, counter_1_carry, EI);
endmodule

module Counter12Wrapper (
  input  CLK,
  input  EI,
  output [3:0] O,
  output out_4
);

  wire counter12_1_eo;

  Counter12 counter12_1 (.CLK(CLK), .EI(EI), .O(O), .EO(counter12_1_eo));
  T_Flip_Flop t_ff_1 (.T(counter12_1_eo), .clk(CLK), .Q(out_4));  // open: Qn, reset, preset
endmodule

module PulseSwitch (
  input  E,
  input  B,
  input  CLK,
  output P
);

  wire d_ff_1_q, d_ff_2_q, d_ff_2_qn;

  D_Flip_Flop d_ff_1 (.D(B), .clk(CLK), .Q(d_ff_1_q));  // open: Qn, preset, reset
  D_Flip_Flop d_ff_2 (.D(d_ff_1_q), .clk(CLK), .Q(d_ff_2_q), .Qn(d_ff_2_qn));  // open: preset, reset
  // NoConnect on d_ff_2_q
  and and_1 (P, E, d_ff_1_q, d_ff_2_qn);
endmodule

module CustomClock (
  input  Mode,
  input  CLK,
  input  MinSet,
  input  HourSet,
  output [3:0] S10,
  output [2:0] S6,
  output [3:0] M10,
  output [2:0] M6,
  output [3:0] H12,
  output AMPM,
  output [3:0] CS10,
  output [3:0] DS10
);

  wire counter6_1_eo, counter6_2_eo, counter10_1_eo, counter10_2_eo, counter10_3_eo, counter10_4_eo,
       not_1_out, or_1_out, or_2_out, pulseswitch_1_p, pulseswitch_2_p;

  Counter10 counter10_1 (.CLK(CLK), .EI(Mode), .O(CS10), .EO(counter10_1_eo));
  Counter10 counter10_2 (.CLK(CLK), .EI(counter10_1_eo), .O(DS10), .EO(counter10_2_eo));
  not not_1 (not_1_out, Mode);
  Counter10 counter10_3 (.CLK(CLK), .EI(counter10_2_eo), .O(S10), .EO(counter10_3_eo));
  Counter6 counter6_1 (.CLK(CLK), .EI(counter10_3_eo), .O(S6), .EO(counter6_1_eo));
  or or_1 (or_1_out, counter6_1_eo, pulseswitch_1_p);
  PulseSwitch pulseswitch_1 (.E(not_1_out), .B(MinSet), .CLK(CLK), .P(pulseswitch_1_p));
  Counter10 counter10_4 (.CLK(CLK), .EI(or_1_out), .O(M10), .EO(counter10_4_eo));
  Counter6 counter6_2 (.CLK(CLK), .EI(counter10_4_eo), .O(M6), .EO(counter6_2_eo));
  or or_2 (or_2_out, counter6_2_eo, pulseswitch_2_p);
  PulseSwitch pulseswitch_2 (.E(not_1_out), .B(HourSet), .CLK(CLK), .P(pulseswitch_2_p));
  Counter12 counter12_1 (.CLK(CLK), .EI(or_2_out), .O(H12), .EO(AMPM));
endmodule

module R0C0Han (
  input  E,
  output [7:0] O0,
  output [7:0] O1,
  output [7:0] O2,
  output [7:0] O3,
  output [7:0] O4,
  output [7:0] O5,
  output [7:0] O6,
  output [7:0] O7
);


  assign O0 = {1'b0, E, 1'b0, E, 4'b0000};
  assign O1 = {1'b0, {2{E}}, 1'b0, E, 3'b000};
  assign O2 = {{3{E}}, 1'b0, E, 3'b000};
  assign O3 = {1'b0, {2{E}}, 1'b0, E, 1'b0, {2{E}}};
  assign O4 = {1'b0, E, 1'b0, E, 3'b000, E};
  assign O5 = {{7{1'b0}}, E};
  assign O6 = {{5{E}}, 2'b00, E};
  assign O7 = {3'b000, E, 4'b0000};
endmodule

module R0C1Doo (
  input  E,
  output [7:0] O0,
  output [7:0] O1,
  output [7:0] O2,
  output [7:0] O3,
  output [7:0] O4,
  output [7:0] O5,
  output [7:0] O6,
  output [7:0] O7
);


  assign O0 = {{5{1'b0}}, E, 2'b00};
  assign O1 = {{4{E}}, 1'b0, E, 2'b00};
  assign O2 = {E, 2'b00, E, 1'b0, E, 2'b00};
  assign O3 = {E, 2'b00, E, 1'b0, {3{E}}};
  assign O4 = {E, 2'b00, E, 1'b0, {3{E}}};
  assign O5 = {E, 2'b00, E, 1'b0, E, 2'b00};
  assign O6 = {E, 2'b00, E, 1'b0, E, 2'b00};
  assign O7 = {{5{1'b0}}, E, 2'b00};
endmodule

module R0C2Se (
  input  E,
  output [7:0] O0,
  output [7:0] O1,
  output [7:0] O2,
  output [7:0] O3,
  output [7:0] O4,
  output [7:0] O5,
  output [7:0] O6,
  output [7:0] O7
);


  assign O0 = {4'b0000, {2{E}}, 2'b00};
  assign O1 = {1'b0, {3{E}}, 4'b0000};
  assign O2 = {4'b0000, {2{E}}, 2'b00};
  assign O3 = {8{1'b0}};
  assign O4 = {3'b000, E, 4'b0000};
  assign O5 = {{7{E}}, 1'b0};
  assign O6 = {8{1'b0}};
  assign O7 = {8{E}};
endmodule

module R0C3Ne (
  input  E,
  output [7:0] O0,
  output [7:0] O1,
  output [7:0] O2,
  output [7:0] O3,
  output [7:0] O4,
  output [7:0] O5,
  output [7:0] O6,
  output [7:0] O7
);


  assign O0 = {{6{E}}, 2'b00};
  assign O1 = {{5{1'b0}}, E, 2'b00};
  assign O2 = {{5{1'b0}}, E, 2'b00};
  assign O3 = {{5{1'b0}}, E, 2'b00};
  assign O4 = {3'b000, E, 4'b0000};
  assign O5 = {{7{E}}, 1'b0};
  assign O6 = {8{1'b0}};
  assign O7 = {8{E}};
endmodule

module R0C4Da (
  input  E,
  output [7:0] O0,
  output [7:0] O1,
  output [7:0] O2,
  output [7:0] O3,
  output [7:0] O4,
  output [7:0] O5,
  output [7:0] O6,
  output [7:0] O7
);


  assign O0 = {1'b0, {6{E}}, 1'b0};
  assign O1 = {1'b0, E, 4'b0000, E, 1'b0};
  assign O2 = {1'b0, E, 4'b0000, E, 1'b0};
  assign O3 = {1'b0, E, 4'b0000, E, 1'b0};
  assign O4 = {1'b0, E, 4'b0000, E, 1'b0};
  assign O5 = {8{1'b0}};
  assign O6 = {8{E}};
  assign O7 = {3'b000, E, 4'b0000};
endmodule

module R0C5Seoc (
  input  E,
  output [7:0] O0,
  output [7:0] O1,
  output [7:0] O2,
  output [7:0] O3,
  output [7:0] O4,
  output [7:0] O5,
  output [7:0] O6,
  output [7:0] O7
);


  assign O0 = {3'b000, E, 4'b0000};
  assign O1 = {2'b00, E, {5{1'b0}}};
  assign O2 = {{2{E}}, {5{1'b0}}, E};
  assign O3 = {2'b00, E, 3'b000, E, 1'b0};
  assign O4 = {3'b000, E, 1'b0, E, 2'b00};
  assign O5 = {{6{1'b0}}, E, 1'b0};
  assign O6 = {2'b00, E, 4'b0000, E};
  assign O7 = {{5{E}}, 3'b000};
endmodule

module R1C0Yu (
  input  E,
  output [7:0] O0,
  output [7:0] O1,
  output [7:0] O2,
  output [7:0] O3,
  output [7:0] O4,
  output [7:0] O5,
  output [7:0] O6,
  output [7:0] O7
);


  assign O0 = {2'b00, {3{E}}, 3'b000};
  assign O1 = {1'b0, E, 3'b000, E, 2'b00};
  assign O2 = {E, {5{1'b0}}, E, 1'b0};
  assign O3 = {E, {5{1'b0}}, E, 1'b0};
  assign O4 = {1'b0, E, 3'b000, E, 2'b00};
  assign O5 = {2'b00, {3{E}}, 3'b000};
  assign O6 = {2'b00, E, 1'b0, E, 3'b000};
  assign O7 = {8{E}};
endmodule

module R1C1Seoc (
  input  E,
  output [7:0] O0,
  output [7:0] O1,
  output [7:0] O2,
  output [7:0] O3,
  output [7:0] O4,
  output [7:0] O5,
  output [7:0] O6,
  output [7:0] O7
);


  assign O0 = {3'b000, E, 4'b0000};
  assign O1 = {2'b00, E, {5{1'b0}}};
  assign O2 = {{2{E}}, {5{1'b0}}, E};
  assign O3 = {2'b00, E, 3'b000, E, 1'b0};
  assign O4 = {3'b000, E, 1'b0, E, 2'b00};
  assign O5 = {{6{1'b0}}, E, 1'b0};
  assign O6 = {2'b00, E, 4'b0000, E};
  assign O7 = {{5{E}}, 3'b000};
endmodule

module R1C2Il (
  input  E,
  output [7:0] O0,
  output [7:0] O1,
  output [7:0] O2,
  output [7:0] O3,
  output [7:0] O4,
  output [7:0] O5,
  output [7:0] O6,
  output [7:0] O7
);


  assign O0 = {1'b0, E, {6{1'b0}}};
  assign O1 = {E, 1'b0, {2{E}}, 1'b0, {3{E}}};
  assign O2 = {E, 1'b0, {2{E}}, 1'b0, E, 1'b0, E};
  assign O3 = {E, 1'b0, {2{E}}, 1'b0, E, 1'b0, E};
  assign O4 = {E, 1'b0, {2{E}}, 1'b0, E, 1'b0, E};
  assign O5 = {1'b0, E, 1'b0, E, 1'b0, E, 1'b0, E};
  assign O6 = {3'b000, E, 1'b0, E, 1'b0, E};
  assign O7 = {{6{E}}, 1'b0, E};
endmodule

module R1C3Goq (
  input  E,
  output [7:0] O0,
  output [7:0] O1,
  output [7:0] O2,
  output [7:0] O3,
  output [7:0] O4,
  output [7:0] O5,
  output [7:0] O6,
  output [7:0] O7
);


  assign O0 = {3'b000, E, 4'b0000};
  assign O1 = {E, 2'b00, {5{E}}};
  assign O2 = {E, 2'b00, E, 1'b0, E, 1'b0, E};
  assign O3 = {E, 1'b0, {2{E}}, 1'b0, E, 1'b0, E};
  assign O4 = {E, 2'b00, E, 1'b0, E, 1'b0, E};
  assign O5 = {E, 2'b00, E, 1'b0, E, 1'b0, E};
  assign O6 = {8{E}};
  assign O7 = {3'b000, E, 4'b0000};
endmodule

module R1C4Yu (
  input  E,
  output [7:0] O0,
  output [7:0] O1,
  output [7:0] O2,
  output [7:0] O3,
  output [7:0] O4,
  output [7:0] O5,
  output [7:0] O6,
  output [7:0] O7
);


  assign O0 = {2'b00, {3{E}}, 3'b000};
  assign O1 = {1'b0, E, 3'b000, E, 2'b00};
  assign O2 = {E, {5{1'b0}}, E, 1'b0};
  assign O3 = {E, {5{1'b0}}, E, 1'b0};
  assign O4 = {1'b0, E, 3'b000, E, 2'b00};
  assign O5 = {2'b00, {3{E}}, 3'b000};
  assign O6 = {2'b00, E, 1'b0, E, 3'b000};
  assign O7 = {8{E}};
endmodule

module R1C5Durb (
  input  E,
  output [7:0] O0,
  output [7:0] O1,
  output [7:0] O2,
  output [7:0] O3,
  output [7:0] O4,
  output [7:0] O5,
  output [7:0] O6,
  output [7:0] O7
);


  assign O0 = {{4{E}}, 1'b0, {3{E}}};
  assign O1 = {E, 1'b0, {2{E}}, 1'b0, E, 1'b0, E};
  assign O2 = {E, 1'b0, {4{E}}, 1'b0, E};
  assign O3 = {E, 1'b0, E, {5{1'b0}}};
  assign O4 = {E, 1'b0, E, 1'b0, {4{E}}};
  assign O5 = {E, 1'b0, E, 2'b00, E, 1'b0, E};
  assign O6 = {1'b0, E, 3'b000, E, 1'b0, E};
  assign O7 = {{3{E}}, 1'b0, {4{E}}};
endmodule

module R2C0A (
  input  E,
  output [7:0] O0,
  output [7:0] O1,
  output [7:0] O2,
  output [7:0] O3,
  output [7:0] O4,
  output [7:0] O5,
  output [7:0] O6,
  output [7:0] O7
);


  assign O0 = {2'b00, {3{E}}, 3'b000};
  assign O1 = {1'b0, E, 3'b000, E, 2'b00};
  assign O2 = {E, {5{1'b0}}, E, 1'b0};
  assign O3 = {E, {5{1'b0}}, E, 1'b0};
  assign O4 = {1'b0, E, 3'b000, E, 2'b00};
  assign O5 = {2'b00, {3{E}}, 3'b000};
  assign O6 = {8{E}};
  assign O7 = {3'b000, E, 4'b0000};
endmodule

module R2C1Hop (
  input  E,
  output [7:0] O0,
  output [7:0] O1,
  output [7:0] O2,
  output [7:0] O3,
  output [7:0] O4,
  output [7:0] O5,
  output [7:0] O6,
  output [7:0] O7
);


  assign O0 = {8{1'b0}};
  assign O1 = {4'b0000, E, 3'b000};
  assign O2 = {1'b0, E, 2'b00, {4{E}}};
  assign O3 = {1'b0, {2{E}}, 1'b0, E, 1'b0, {2{E}}};
  assign O4 = {{5{E}}, 1'b0, {2{E}}};
  assign O5 = {1'b0, {2{E}}, 1'b0, E, 1'b0, {2{E}}};
  assign O6 = {1'b0, E, 2'b00, {4{E}}};
  assign O7 = {4'b0000, E, 3'b000};
endmodule

module R2C2Yul (
  input  E,
  output [7:0] O0,
  output [7:0] O1,
  output [7:0] O2,
  output [7:0] O3,
  output [7:0] O4,
  output [7:0] O5,
  output [7:0] O6,
  output [7:0] O7
);


  assign O0 = {1'b0, E, {6{1'b0}}};
  assign O1 = {E, 1'b0, {2{E}}, 1'b0, {3{E}}};
  assign O2 = {E, 1'b0, {2{E}}, 1'b0, E, 1'b0, E};
  assign O3 = {E, 1'b0, {2{E}}, 1'b0, E, 1'b0, E};
  assign O4 = {1'b0, E, 1'b0, E, 1'b0, E, 1'b0, E};
  assign O5 = {3'b000, E, 1'b0, E, 1'b0, E};
  assign O6 = {{2{E}}, 1'b0, E, 1'b0, E, 1'b0, E};
  assign O7 = {{6{E}}, 1'b0, E};
endmodule

module R2C3Han (
  input  E,
  output [7:0] O0,
  output [7:0] O1,
  output [7:0] O2,
  output [7:0] O3,
  output [7:0] O4,
  output [7:0] O5,
  output [7:0] O6,
  output [7:0] O7
);


  assign O0 = {1'b0, E, 1'b0, E, 4'b0000};
  assign O1 = {1'b0, {2{E}}, 1'b0, E, 3'b000};
  assign O2 = {{3{E}}, 1'b0, E, 3'b000};
  assign O3 = {1'b0, {2{E}}, 1'b0, E, 1'b0, {2{E}}};
  assign O4 = {1'b0, E, 1'b0, E, 3'b000, E};
  assign O5 = {{7{1'b0}}, E};
  assign O6 = {{5{E}}, 2'b00, E};
  assign O7 = {3'b000, E, 4'b0000};
endmodule

module R2C4Doo (
  input  E,
  output [7:0] O0,
  output [7:0] O1,
  output [7:0] O2,
  output [7:0] O3,
  output [7:0] O4,
  output [7:0] O5,
  output [7:0] O6,
  output [7:0] O7
);


  assign O0 = {{5{1'b0}}, E, 2'b00};
  assign O1 = {{4{E}}, 1'b0, E, 2'b00};
  assign O2 = {E, 2'b00, E, 1'b0, E, 2'b00};
  assign O3 = {E, 2'b00, E, 1'b0, {3{E}}};
  assign O4 = {E, 2'b00, E, 1'b0, {3{E}}};
  assign O5 = {E, 2'b00, E, 1'b0, E, 2'b00};
  assign O6 = {E, 2'b00, E, 1'b0, E, 2'b00};
  assign O7 = {{5{1'b0}}, E, 2'b00};
endmodule

module R2C5Si (
  input  E,
  output [7:0] O0,
  output [7:0] O1,
  output [7:0] O2,
  output [7:0] O3,
  output [7:0] O4,
  output [7:0] O5,
  output [7:0] O6,
  output [7:0] O7
);


  assign O0 = {{7{1'b0}}, E};
  assign O1 = {{6{1'b0}}, E, 1'b0};
  assign O2 = {{5{1'b0}}, E, 2'b00};
  assign O3 = {{5{E}}, 3'b000};
  assign O4 = {{5{1'b0}}, E, 2'b00};
  assign O5 = {{6{1'b0}}, E, 1'b0};
  assign O6 = {{7{1'b0}}, E};
  assign O7 = {8{E}};
endmodule

module R3C0Ja (
  input  E,
  output [7:0] O0,
  output [7:0] O1,
  output [7:0] O2,
  output [7:0] O3,
  output [7:0] O4,
  output [7:0] O5,
  output [7:0] O6,
  output [7:0] O7
);


  assign O0 = {1'b0, E, 4'b0000, E, 1'b0};
  assign O1 = {1'b0, E, 3'b000, E, 2'b00};
  assign O2 = {1'b0, {4{E}}, 3'b000};
  assign O3 = {1'b0, E, 3'b000, E, 2'b00};
  assign O4 = {1'b0, E, 4'b0000, E, 1'b0};
  assign O5 = {8{1'b0}};
  assign O6 = {8{E}};
  assign O7 = {3'b000, E, 4'b0000};
endmodule

module R3C1Yi (
  input  E,
  output [7:0] O0,
  output [7:0] O1,
  output [7:0] O2,
  output [7:0] O3,
  output [7:0] O4,
  output [7:0] O5,
  output [7:0] O6,
  output [7:0] O7
);


  assign O0 = {3'b000, {2{E}}, 3'b000};
  assign O1 = {2'b00, E, 2'b00, E, 2'b00};
  assign O2 = {1'b0, E, 4'b0000, E, 1'b0};
  assign O3 = {1'b0, E, 4'b0000, E, 1'b0};
  assign O4 = {2'b00, E, 2'b00, E, 2'b00};
  assign O5 = {3'b000, {2{E}}, 3'b000};
  assign O6 = {8{1'b0}};
  assign O7 = {8{E}};
endmodule

module R3C2Sam (
  input  E,
  output [7:0] O0,
  output [7:0] O1,
  output [7:0] O2,
  output [7:0] O3,
  output [7:0] O4,
  output [7:0] O5,
  output [7:0] O6,
  output [7:0] O7
);


  assign O0 = {2'b00, E, 2'b00, {3{E}}};
  assign O1 = {1'b0, E, 3'b000, E, 1'b0, E};
  assign O2 = {E, 4'b0000, E, 1'b0, E};
  assign O3 = {1'b0, E, 3'b000, E, 1'b0, E};
  assign O4 = {2'b00, E, 2'b00, E, 1'b0, E};
  assign O5 = {{5{1'b0}}, E, 1'b0, E};
  assign O6 = {{3{E}}, 2'b00, E, 1'b0, E};
  assign O7 = {1'b0, E, 3'b000, {3{E}}};
endmodule

module R3C3Sa (
  input  E,
  output [7:0] O0,
  output [7:0] O1,
  output [7:0] O2,
  output [7:0] O3,
  output [7:0] O4,
  output [7:0] O5,
  output [7:0] O6,
  output [7:0] O7
);


  assign O0 = {{6{1'b0}}, E, 1'b0};
  assign O1 = {{5{1'b0}}, E, 2'b00};
  assign O2 = {1'b0, {4{E}}, 3'b000};
  assign O3 = {{5{1'b0}}, E, 2'b00};
  assign O4 = {{6{1'b0}}, E, 1'b0};
  assign O5 = {8{1'b0}};
  assign O6 = {8{E}};
  assign O7 = {3'b000, E, 4'b0000};
endmodule

module R3C4O (
  input  E,
  output [7:0] O0,
  output [7:0] O1,
  output [7:0] O2,
  output [7:0] O3,
  output [7:0] O4,
  output [7:0] O5,
  output [7:0] O6,
  output [7:0] O7
);


  assign O0 = {2'b00, {2{E}}, 3'b000, E};
  assign O1 = {1'b0, E, 2'b00, E, 2'b00, E};
  assign O2 = {E, 4'b0000, E, 1'b0, E};
  assign O3 = {E, 4'b0000, {3{E}}};
  assign O4 = {E, 4'b0000, E, 1'b0, E};
  assign O5 = {1'b0, E, 2'b00, E, 2'b00, E};
  assign O6 = {2'b00, {2{E}}, 3'b000, E};
  assign O7 = {8{1'b0}};
endmodule

module R3C5Siq (
  input  E,
  output [7:0] O0,
  output [7:0] O1,
  output [7:0] O2,
  output [7:0] O3,
  output [7:0] O4,
  output [7:0] O5,
  output [7:0] O6,
  output [7:0] O7
);


  assign O0 = {3'b000, {5{E}}};
  assign O1 = {2'b00, E, 2'b00, E, 1'b0, E};
  assign O2 = {1'b0, E, 3'b000, E, 1'b0, E};
  assign O3 = {E, 4'b0000, E, 1'b0, E};
  assign O4 = {1'b0, E, 3'b000, E, 1'b0, E};
  assign O5 = {2'b00, E, 2'b00, E, 1'b0, E};
  assign O6 = {{5{1'b0}}, E, 1'b0, E};
  assign O7 = {{3{E}}, 1'b0, {4{E}}};
endmodule

module R4C0Jeong (
  input  E,
  output [7:0] O0,
  output [7:0] O1,
  output [7:0] O2,
  output [7:0] O3,
  output [7:0] O4,
  output [7:0] O5,
  output [7:0] O6,
  output [7:0] O7
);


  assign O0 = {E, 2'b00, E, 4'b0000};
  assign O1 = {E, 1'b0, E, 3'b000, E, 1'b0};
  assign O2 = {{2{E}}, 3'b000, E, 1'b0, E};
  assign O3 = {E, 1'b0, E, 2'b00, E, 1'b0, E};
  assign O4 = {E, 2'b00, E, 1'b0, E, 1'b0, E};
  assign O5 = {{5{1'b0}}, E, 1'b0, E};
  assign O6 = {1'b0, E, 4'b0000, E, 1'b0};
  assign O7 = {{3{E}}, {5{1'b0}}};
endmodule

module R4C1Il (
  input  E,
  output [7:0] O0,
  output [7:0] O1,
  output [7:0] O2,
  output [7:0] O3,
  output [7:0] O4,
  output [7:0] O5,
  output [7:0] O6,
  output [7:0] O7
);


  assign O0 = {1'b0, E, {6{1'b0}}};
  assign O1 = {E, 1'b0, {2{E}}, 1'b0, {3{E}}};
  assign O2 = {E, 1'b0, {2{E}}, 1'b0, E, 1'b0, E};
  assign O3 = {E, 1'b0, {2{E}}, 1'b0, E, 1'b0, E};
  assign O4 = {E, 1'b0, {2{E}}, 1'b0, E, 1'b0, E};
  assign O5 = {1'b0, E, 1'b0, E, 1'b0, E, 1'b0, E};
  assign O6 = {3'b000, E, 1'b0, E, 1'b0, E};
  assign O7 = {{6{E}}, 1'b0, E};
endmodule

module R4C2Yi (
  input  E,
  output [7:0] O0,
  output [7:0] O1,
  output [7:0] O2,
  output [7:0] O3,
  output [7:0] O4,
  output [7:0] O5,
  output [7:0] O6,
  output [7:0] O7
);


  assign O0 = {3'b000, {2{E}}, 3'b000};
  assign O1 = {2'b00, E, 2'b00, E, 2'b00};
  assign O2 = {1'b0, E, 4'b0000, E, 1'b0};
  assign O3 = {1'b0, E, 4'b0000, E, 1'b0};
  assign O4 = {2'b00, E, 2'b00, E, 2'b00};
  assign O5 = {3'b000, {2{E}}, 3'b000};
  assign O6 = {8{1'b0}};
  assign O7 = {8{E}};
endmodule

module R4C3Sam (
  input  E,
  output [7:0] O0,
  output [7:0] O1,
  output [7:0] O2,
  output [7:0] O3,
  output [7:0] O4,
  output [7:0] O5,
  output [7:0] O6,
  output [7:0] O7
);


  assign O0 = {2'b00, E, 2'b00, {3{E}}};
  assign O1 = {1'b0, E, 3'b000, E, 1'b0, E};
  assign O2 = {E, 4'b0000, E, 1'b0, E};
  assign O3 = {1'b0, E, 3'b000, E, 1'b0, E};
  assign O4 = {2'b00, E, 2'b00, E, 1'b0, E};
  assign O5 = {{5{1'b0}}, E, 1'b0, E};
  assign O6 = {{3{E}}, 2'b00, E, 1'b0, E};
  assign O7 = {1'b0, E, 3'b000, {3{E}}};
endmodule

module R4C4Sa (
  input  E,
  output [7:0] O0,
  output [7:0] O1,
  output [7:0] O2,
  output [7:0] O3,
  output [7:0] O4,
  output [7:0] O5,
  output [7:0] O6,
  output [7:0] O7
);


  assign O0 = {{6{1'b0}}, E, 1'b0};
  assign O1 = {{5{1'b0}}, E, 2'b00};
  assign O2 = {1'b0, {4{E}}, 3'b000};
  assign O3 = {{5{1'b0}}, E, 2'b00};
  assign O4 = {{6{1'b0}}, E, 1'b0};
  assign O5 = {8{1'b0}};
  assign O6 = {8{E}};
  assign O7 = {3'b000, E, 4'b0000};
endmodule

module R4C5Yuk (
  input  E,
  output [7:0] O0,
  output [7:0] O1,
  output [7:0] O2,
  output [7:0] O3,
  output [7:0] O4,
  output [7:0] O5,
  output [7:0] O6,
  output [7:0] O7
);


  assign O0 = {1'b0, E, 2'b00, E, 1'b0, E, 1'b0};
  assign O1 = {E, 1'b0, E, 1'b0, E, 1'b0, E, 1'b0};
  assign O2 = {E, 1'b0, E, 1'b0, {3{E}}, 1'b0};
  assign O3 = {E, 1'b0, E, 1'b0, E, 1'b0, E, 1'b0};
  assign O4 = {E, 1'b0, E, 1'b0, E, 1'b0, E, 1'b0};
  assign O5 = {E, 1'b0, E, 1'b0, {3{E}}, 1'b0};
  assign O6 = {E, 1'b0, E, 1'b0, E, 1'b0, E, 1'b0};
  assign O7 = {1'b0, E, 2'b00, E, 1'b0, {2{E}}};
endmodule

module R5C0O (
  input  E,
  output [7:0] O0,
  output [7:0] O1,
  output [7:0] O2,
  output [7:0] O3,
  output [7:0] O4,
  output [7:0] O5,
  output [7:0] O6,
  output [7:0] O7
);


  assign O0 = {2'b00, {2{E}}, 3'b000, E};
  assign O1 = {1'b0, E, 2'b00, E, 2'b00, E};
  assign O2 = {E, 4'b0000, E, 1'b0, E};
  assign O3 = {E, 4'b0000, {3{E}}};
  assign O4 = {E, 4'b0000, E, 1'b0, E};
  assign O5 = {1'b0, E, 2'b00, E, 2'b00, E};
  assign O6 = {2'b00, {2{E}}, 3'b000, E};
  assign O7 = {8{1'b0}};
endmodule

module R5C1O (
  input  E,
  output [7:0] O0,
  output [7:0] O1,
  output [7:0] O2,
  output [7:0] O3,
  output [7:0] O4,
  output [7:0] O5,
  output [7:0] O6,
  output [7:0] O7
);


  assign O0 = {2'b00, {2{E}}, 3'b000, E};
  assign O1 = {1'b0, E, 2'b00, E, 2'b00, E};
  assign O2 = {E, 4'b0000, E, 1'b0, E};
  assign O3 = {E, 4'b0000, {3{E}}};
  assign O4 = {E, 4'b0000, E, 1'b0, E};
  assign O5 = {1'b0, E, 2'b00, E, 2'b00, E};
  assign O6 = {2'b00, {2{E}}, 3'b000, E};
  assign O7 = {8{1'b0}};
endmodule

module R5C2Chil (
  input  E,
  output [7:0] O0,
  output [7:0] O1,
  output [7:0] O2,
  output [7:0] O3,
  output [7:0] O4,
  output [7:0] O5,
  output [7:0] O6,
  output [7:0] O7
);


  assign O0 = {4'b0000, E, 1'b0, {2{E}}};
  assign O1 = {1'b0, E, 2'b00, E, 1'b0, {2{E}}};
  assign O2 = {1'b0, E, 1'b0, {2{E}}, 1'b0, {2{E}}};
  assign O3 = {{3{E}}, 1'b0, E, 1'b0, {2{E}}};
  assign O4 = {1'b0, E, 1'b0, {2{E}}, 1'b0, {2{E}}};
  assign O5 = {1'b0, E, 2'b00, E, 1'b0, {2{E}}};
  assign O6 = {4'b0000, E, 1'b0, {2{E}}};
  assign O7 = {8{E}};
endmodule

module R5C3Pal (
  input  E,
  output [7:0] O0,
  output [7:0] O1,
  output [7:0] O2,
  output [7:0] O3,
  output [7:0] O4,
  output [7:0] O5,
  output [7:0] O6,
  output [7:0] O7
);


  assign O0 = {E, 1'b0, E, 1'b0, E, 1'b0, {2{E}}};
  assign O1 = {{3{E}}, 1'b0, E, 1'b0, {2{E}}};
  assign O2 = {E, 1'b0, E, 1'b0, E, 1'b0, {2{E}}};
  assign O3 = {{3{E}}, 1'b0, E, 1'b0, {2{E}}};
  assign O4 = {E, 1'b0, E, 1'b0, E, 1'b0, {2{E}}};
  assign O5 = {4'b0000, E, 1'b0, {2{E}}};
  assign O6 = {{5{E}}, 1'b0, {2{E}}};
  assign O7 = {1'b0, E, 2'b00, {4{E}}};
endmodule

module R5C4Koo (
  input  E,
  output [7:0] O0,
  output [7:0] O1,
  output [7:0] O2,
  output [7:0] O3,
  output [7:0] O4,
  output [7:0] O5,
  output [7:0] O6,
  output [7:0] O7
);


  assign O0 = {{5{1'b0}}, E, 2'b00};
  assign O1 = {E, 4'b0000, E, 2'b00};
  assign O2 = {E, 4'b0000, E, 2'b00};
  assign O3 = {E, 4'b0000, {3{E}}};
  assign O4 = {E, 4'b0000, {3{E}}};
  assign O5 = {E, 4'b0000, E, 2'b00};
  assign O6 = {{6{E}}, 2'b00};
  assign O7 = {{5{1'b0}}, E, 2'b00};
endmodule

module R5C5Boon (
  input  E,
  output [7:0] O0,
  output [7:0] O1,
  output [7:0] O2,
  output [7:0] O3,
  output [7:0] O4,
  output [7:0] O5,
  output [7:0] O6,
  output [7:0] O7
);


  assign O0 = {{5{1'b0}}, {3{E}}};
  assign O1 = {{4{E}}, 1'b0, E, 1'b0, E};
  assign O2 = {1'b0, E, 1'b0, E, 1'b0, E, 1'b0, E};
  assign O3 = {1'b0, E, 1'b0, E, 1'b0, {3{E}}};
  assign O4 = {1'b0, E, 1'b0, E, 1'b0, {3{E}}};
  assign O5 = {1'b0, E, 1'b0, E, 1'b0, E, 1'b0, E};
  assign O6 = {{4{E}}, 1'b0, E, 1'b0, E};
  assign O7 = {{5{1'b0}}, E, 1'b0, E};
endmodule

module Viewer (
  input  Mode,
  input  CLK,
  input  MinSet,
  input  HourSet,
  output R0C0,
  output R0C1,
  output R0C2,
  output R0C3,
  output R0C4,
  output R0C5,
  output R1C0,
  output R1C1,
  output R1C2,
  output R1C3,
  output R1C4,
  output R1C5,
  output R2C0,
  output R2C1,
  output R2C2,
  output R2C3,
  output R2C4,
  output R2C5,
  output R3C0,
  output R3C1,
  output R3C2,
  output R3C3,
  output R3C4,
  output R3C5,
  output R4C0,
  output R4C1,
  output R4C2,
  output R4C3,
  output R4C4,
  output R4C5,
  output R5C0,
  output R5C1,
  output R5C2,
  output R5C3,
  output R5C4,
  output R5C5,
  output [3:0] S10,
  output [3:0] S6,
  output [3:0] M10,
  output [3:0] M6,
  output [3:0] H2,
  output [3:0] H10,
  output [3:0] CS10,
  output [3:0] DS10
);

  wire customclock_1_ampm, h12decoder_1_o12h0, m6decoder_1_o6m0, m10decoder_1_o10m0;
  wire [2:0] customclock_1_m6, customclock_1_s6;
  wire [3:0] customclock_1_cs10, customclock_1_ds10, customclock_1_h12, customclock_1_m10, customclock_1_s10;

  CustomClock customclock_1 (
    .Mode(Mode), .CLK(CLK), .MinSet(MinSet), .HourSet(HourSet), .S10(customclock_1_s10),
    .S6(customclock_1_s6), .M10(customclock_1_m10), .M6(customclock_1_m6), .H12(customclock_1_h12),
    .AMPM(customclock_1_ampm), .CS10(customclock_1_cs10), .DS10(customclock_1_ds10));
  // Binary_to_BCD_converter #(.binvalue(4)) binary_to_bcd_converter_1: pin names not known; wires that end beside it: customclock_1_s10, S10
  // Binary_to_BCD_converter #(.binvalue(4)) binary_to_bcd_converter_2: pin names not known; wires that end beside it: customclock_1_cs10, CS10
  // Binary_to_BCD_converter #(.binvalue(4)) binary_to_bcd_converter_3: pin names not known; wires that end beside it: S6
  // Binary_to_BCD_converter #(.binvalue(4)) binary_to_bcd_converter_4: pin names not known; wires that end beside it: customclock_1_ds10, DS10
  H12Decoder h12decoder_1 (
    .IH12(customclock_1_h12), .R0C0(R0C0), .R0C1(R0C1), .R0C2(R0C2), .R0C3(R0C3), .R0C4(R0C4), .R0C5(R0C5),
    .R1C0(R1C0), .R1C1(R1C1), .R1C2(R1C2), .R1C3(R1C3), .R1C4(R1C4), .R1C5(R1C5), .R2C0(R2C0), .R2C1(R2C1),
    .R2C2(R2C2), .R2C3(R2C3), .R2C4(R2C4), .R2C5(R2C5), .O12H0(h12decoder_1_o12h0));
  M6Decoder m6decoder_1 (
    .IM6(customclock_1_m6), .R3C1(R3C1), .R3C2(R3C2), .R3C3(R3C3), .R3C4(R3C4), .R3C5(R3C5),
    .O6M0(m6decoder_1_o6m0));
  M10Decoder m10decoder_1 (
    .IM10(customclock_1_m10), .R4C1(R4C1), .R4C2(R4C2), .R4C3(R4C3), .R4C4(R4C4), .R4C5(R4C5), .R5C1(R5C1),
    .R5C2(R5C2), .R5C3(R5C3), .R5C4(R5C4), .R5C5(R5C5), .O10M0(m10decoder_1_o10m0));
  // Binary_to_BCD_converter #(.binvalue(4)) binary_to_bcd_converter_5: pin names not known; wires that end beside it: customclock_1_m10, M10
  and and_1 (R4C0, h12decoder_1_o12h0, m10decoder_1_o10m0, m6decoder_1_o6m0);
  // Binary_to_BCD_converter #(.binvalue(4)) binary_to_bcd_converter_6: pin names not known; wires that end beside it: M6
  and and_2 (R3C0, R4C0, ~customclock_1_ampm);  // AND_Gate
  and and_3 (R5C0, R4C0, customclock_1_ampm);
  // Binary_to_BCD_converter #(.binvalue(4)) binary_to_bcd_converter_7: pin names not known; wires that end beside it: customclock_1_h12, customclock_1_ampm, H10, H2
endmodule

module H12Decoder (
  input  [3:0] IH12,
  output R0C0,
  output R0C1,
  output R0C2,
  output R0C3,
  output R0C4,
  output R0C5,
  output R1C0,
  output R1C1,
  output R1C2,
  output R1C3,
  output R1C4,
  output R1C5,
  output R2C0,
  output R2C1,
  output R2C2,
  output R2C3,
  output R2C4,
  output R2C5,
  output O12H0
);

  wire demultiplexer_1_out10, demultiplexer_1_out12;

  Demultiplexer #(.select(4)) demultiplexer_1 (
    .out0(O12H0), .out1(R0C0), .out2(R0C1), .out3(R0C2), .out4(R0C3), .out5(R0C4), .out6(R1C0), .out7(R1C2),
    .out8(R1C4), .out9(R2C0), .out10(demultiplexer_1_out10), .out11(R2C3), .out12(demultiplexer_1_out12),
    .out13(demultiplexer_1_out12), .out14(demultiplexer_1_out12), .out15(demultiplexer_1_out12), .in(1'b1),
    .sel(IH12));
  // NoConnect on demultiplexer_1_out12
  or or_1 (R2C2, R2C3, demultiplexer_1_out10, O12H0);

  assign R0C5 = R0C4;
  assign R1C1 = R1C0;
  assign R1C3 = R1C2;
  assign R1C5 = R1C4;
  assign R2C1 = R2C0;
  assign R2C4 = O12H0;
  assign R2C5 = 1'b1;
endmodule

module M6Decoder (
  input  [2:0] IM6,
  output R3C1,
  output R3C2,
  output R3C3,
  output R3C4,
  output R3C5,
  output O6M0
);

  wire demultiplexer_1_out1, demultiplexer_1_out6;

  Demultiplexer #(.select(3)) demultiplexer_1 (
    .out0(O6M0), .out1(demultiplexer_1_out1), .out2(R3C1), .out3(R3C2), .out4(R3C3), .out5(R3C4),
    .out6(demultiplexer_1_out6), .out7(demultiplexer_1_out6), .in(1'b1), .sel(IM6));
  // NoConnect on demultiplexer_1_out6
  or or_1 (R3C5, R3C4, R3C3, R3C2, R3C1, demultiplexer_1_out1);
endmodule

module M10Decoder (
  input  [3:0] IM10,
  output R4C1,
  output R4C2,
  output R4C3,
  output R4C4,
  output R4C5,
  output R5C1,
  output R5C2,
  output R5C3,
  output R5C4,
  output R5C5,
  output O10M0
);

  Demultiplexer #(.select(4)) demultiplexer_1 (
    .out0(O10M0), .out1(R4C1), .out2(R4C2), .out3(R4C3), .out4(R4C4), .out5(R5C1), .out6(R4C5), .out7(R5C2),
    .out8(R5C3), .out9(R5C4), .in(1'b1), .sel(IM10));  // open: out10, out11, out12, out13, out14, out15
  not not_1 (R5C5, O10M0);
endmodule

module test (
  input  Mode
);

  wire button_1_out, button_2_out, clock_1_out, R0C0, R0C1, R0C2, R0C3, R0C4, R0C5, R1C0, R1C1, R1C2, R1C3,
       R1C4, R1C5, R2C0, R2C1, R2C2, R2C3, R2C4, R2C5, R3C0, R3C1, R3C2, R3C3, R3C4, R3C5, R4C0, R4C1, R4C2,
       R4C3, R4C4, R4C5, R5C0, R5C1, R5C2, R5C3, R5C4, R5C5;
  wire [3:0] n7_segment_display_1_p1, n7_segment_display_1_p2, viewer_1_m6, viewer_1_m10, viewer_1_s6,
       viewer_1_s10;
  wire [7:0] r0c0han_1_o0, r0c0han_1_o1, r0c0han_1_o2, r0c0han_1_o3, r0c0han_1_o4, r0c0han_1_o5,
       r0c0han_1_o6, r0c0han_1_o7, r0c1doo_1_o0, r0c1doo_1_o1, r0c1doo_1_o2, r0c1doo_1_o3, r0c1doo_1_o4,
       r0c1doo_1_o5, r0c1doo_1_o6, r0c1doo_1_o7, r0c2se_1_o0, r0c2se_1_o1, r0c2se_1_o2, r0c2se_1_o3,
       r0c2se_1_o4, r0c2se_1_o5, r0c2se_1_o6, r0c2se_1_o7, r0c3ne_1_o0, r0c3ne_1_o1, r0c3ne_1_o2,
       r0c3ne_1_o3, r0c3ne_1_o4, r0c3ne_1_o5, r0c3ne_1_o6, r0c3ne_1_o7, r0c4da_1_o0, r0c4da_1_o1,
       r0c4da_1_o2, r0c4da_1_o3, r0c4da_1_o4, r0c4da_1_o5, r0c4da_1_o6, r0c4da_1_o7, r0c5seoc_1_o0,
       r0c5seoc_1_o1, r0c5seoc_1_o2, r0c5seoc_1_o3, r0c5seoc_1_o4, r0c5seoc_1_o5, r0c5seoc_1_o6,
       r0c5seoc_1_o7, r1c0yu_1_o0, r1c0yu_1_o1, r1c0yu_1_o2, r1c0yu_1_o3, r1c0yu_1_o4, r1c0yu_1_o5,
       r1c0yu_1_o6, r1c0yu_1_o7, r1c1seoc_1_o0, r1c1seoc_1_o1, r1c1seoc_1_o2, r1c1seoc_1_o3, r1c1seoc_1_o4,
       r1c1seoc_1_o5, r1c1seoc_1_o6, r1c1seoc_1_o7, r1c2il_1_o0, r1c2il_1_o1, r1c2il_1_o2, r1c2il_1_o3,
       r1c2il_1_o4, r1c2il_1_o5, r1c2il_1_o6, r1c2il_1_o7, r1c3goq_1_o0, r1c3goq_1_o1, r1c3goq_1_o2,
       r1c3goq_1_o3, r1c3goq_1_o4, r1c3goq_1_o5, r1c3goq_1_o6, r1c3goq_1_o7, r1c4yu_1_o0, r1c4yu_1_o1,
       r1c4yu_1_o2, r1c4yu_1_o3, r1c4yu_1_o4, r1c4yu_1_o5, r1c4yu_1_o6, r1c4yu_1_o7, r1c5durb_1_o0,
       r1c5durb_1_o1, r1c5durb_1_o2, r1c5durb_1_o3, r1c5durb_1_o4, r1c5durb_1_o5, r1c5durb_1_o6,
       r1c5durb_1_o7, r2c0a_1_o0, r2c0a_1_o1, r2c0a_1_o2, r2c0a_1_o3, r2c0a_1_o4, r2c0a_1_o5, r2c0a_1_o6,
       r2c0a_1_o7, r2c1hop_1_o0, r2c1hop_1_o1, r2c1hop_1_o2, r2c1hop_1_o3, r2c1hop_1_o4, r2c1hop_1_o5,
       r2c1hop_1_o6, r2c1hop_1_o7, r2c2yul_1_o0, r2c2yul_1_o1, r2c2yul_1_o2, r2c2yul_1_o3, r2c2yul_1_o4,
       r2c2yul_1_o5, r2c2yul_1_o6, r2c2yul_1_o7, r2c3han_1_o0, r2c3han_1_o1, r2c3han_1_o2, r2c3han_1_o3,
       r2c3han_1_o4, r2c3han_1_o5, r2c3han_1_o6, r2c3han_1_o7, r2c4doo_1_o0, r2c4doo_1_o1, r2c4doo_1_o2,
       r2c4doo_1_o3, r2c4doo_1_o4, r2c4doo_1_o5, r2c4doo_1_o6, r2c4doo_1_o7, r2c5si_1_o0, r2c5si_1_o1,
       r2c5si_1_o2, r2c5si_1_o3, r2c5si_1_o4, r2c5si_1_o5, r2c5si_1_o6, r2c5si_1_o7, r3c0ja_1_o0,
       r3c0ja_1_o1, r3c0ja_1_o2, r3c0ja_1_o3, r3c0ja_1_o4, r3c0ja_1_o5, r3c0ja_1_o6, r3c0ja_1_o7,
       r3c1yi_1_o0, r3c1yi_1_o1, r3c1yi_1_o2, r3c1yi_1_o3, r3c1yi_1_o4, r3c1yi_1_o5, r3c1yi_1_o6,
       r3c1yi_1_o7, r3c2sam_1_o0, r3c2sam_1_o1, r3c2sam_1_o2, r3c2sam_1_o3, r3c2sam_1_o4, r3c2sam_1_o5,
       r3c2sam_1_o6, r3c2sam_1_o7, r3c3sa_1_o0, r3c3sa_1_o1, r3c3sa_1_o2, r3c3sa_1_o3, r3c3sa_1_o4,
       r3c3sa_1_o5, r3c3sa_1_o6, r3c3sa_1_o7, r3c4o_1_o0, r3c4o_1_o1, r3c4o_1_o2, r3c4o_1_o3, r3c4o_1_o4,
       r3c4o_1_o5, r3c4o_1_o6, r3c4o_1_o7, r3c5siq_1_o0, r3c5siq_1_o1, r3c5siq_1_o2, r3c5siq_1_o3,
       r3c5siq_1_o4, r3c5siq_1_o5, r3c5siq_1_o6, r3c5siq_1_o7, r4c0jeong_1_o0, r4c0jeong_1_o1,
       r4c0jeong_1_o2, r4c0jeong_1_o3, r4c0jeong_1_o4, r4c0jeong_1_o5, r4c0jeong_1_o6, r4c0jeong_1_o7,
       r4c1il_1_o0, r4c1il_1_o1, r4c1il_1_o2, r4c1il_1_o3, r4c1il_1_o4, r4c1il_1_o5, r4c1il_1_o6,
       r4c1il_1_o7, r4c2yi_1_o0, r4c2yi_1_o1, r4c2yi_1_o2, r4c2yi_1_o3, r4c2yi_1_o4, r4c2yi_1_o5,
       r4c2yi_1_o6, r4c2yi_1_o7, r4c3sam_1_o0, r4c3sam_1_o1, r4c3sam_1_o2, r4c3sam_1_o3, r4c3sam_1_o4,
       r4c3sam_1_o5, r4c3sam_1_o6, r4c3sam_1_o7, r4c4sa_1_o0, r4c4sa_1_o1, r4c4sa_1_o2, r4c4sa_1_o3,
       r4c4sa_1_o4, r4c4sa_1_o5, r4c4sa_1_o6, r4c4sa_1_o7, r4c5yuk_1_o0, r4c5yuk_1_o1, r4c5yuk_1_o2,
       r4c5yuk_1_o3, r4c5yuk_1_o4, r4c5yuk_1_o5, r4c5yuk_1_o6, r4c5yuk_1_o7, r5c0o_1_o0, r5c0o_1_o1,
       r5c0o_1_o2, r5c0o_1_o3, r5c0o_1_o4, r5c0o_1_o5, r5c0o_1_o6, r5c0o_1_o7, r5c1o_1_o0, r5c1o_1_o1,
       r5c1o_1_o2, r5c1o_1_o3, r5c1o_1_o4, r5c1o_1_o5, r5c1o_1_o6, r5c1o_1_o7, r5c2chil_1_o0, r5c2chil_1_o1,
       r5c2chil_1_o2, r5c2chil_1_o3, r5c2chil_1_o4, r5c2chil_1_o5, r5c2chil_1_o6, r5c2chil_1_o7,
       r5c3pal_1_o0, r5c3pal_1_o1, r5c3pal_1_o2, r5c3pal_1_o3, r5c3pal_1_o4, r5c3pal_1_o5, r5c3pal_1_o6,
       r5c3pal_1_o7, r5c4koo_1_o0, r5c4koo_1_o1, r5c4koo_1_o2, r5c4koo_1_o3, r5c4koo_1_o4, r5c4koo_1_o5,
       r5c4koo_1_o6, r5c4koo_1_o7, r5c5boon_1_o0, r5c5boon_1_o1, r5c5boon_1_o2, r5c5boon_1_o3, r5c5boon_1_o4,
       r5c5boon_1_o5, r5c5boon_1_o6, r5c5boon_1_o7;

  Clock clock_1 (.out(clock_1_out));
  Button button_1 (.out(button_1_out));
  // _7_Segment_Display 7_segment_display_1: pin names not known; wires that end beside it: n7_segment_display_1_p1, n7_segment_display_1_p2
  _7_Segment_Display u_7_segment_display_2 ();  // open: g, f, a, b, e, d, c, dp
  // BCD_to_7_Segment_decoder bcd_to_7_segment_decoder_1: pin names not known
  // BCD_to_7_Segment_decoder bcd_to_7_segment_decoder_2: pin names not known
  Viewer viewer_1 (
    .Mode(Mode), .CLK(clock_1_out), .MinSet(button_2_out), .HourSet(button_1_out), .R0C0(R0C0), .R0C1(R0C1),
    .R0C2(R0C2), .R0C3(R0C3), .R0C4(R0C4), .R0C5(R0C5), .R1C0(R1C0), .R1C1(R1C1), .R1C2(R1C2), .R1C3(R1C3),
    .R1C4(R1C4), .R1C5(R1C5), .R2C0(R2C0), .R2C1(R2C1), .R2C2(R2C2), .R2C3(R2C3), .R2C4(R2C4), .R2C5(R2C5),
    .R3C0(R3C0), .R3C1(R3C1), .R3C2(R3C2), .R3C3(R3C3), .R3C4(R3C4), .R3C5(R3C5), .R4C0(R4C0), .R4C1(R4C1),
    .R4C2(R4C2), .R4C3(R4C3), .R4C4(R4C4), .R4C5(R4C5), .R5C0(R5C0), .R5C1(R5C1), .R5C2(R5C2), .R5C3(R5C3),
    .R5C4(R5C4), .R5C5(R5C5), .S10(viewer_1_s10), .S6(viewer_1_s6), .M10(viewer_1_m10), .M6(viewer_1_m6),
    .H2(n7_segment_display_1_p2), .H10(n7_segment_display_1_p1));  // open: CS10, DS10
  // _7_Segment_Display 7_segment_display_3: pin names not known; wires that end beside it: viewer_1_m6, viewer_1_m10
  // BCD_to_7_Segment_decoder bcd_to_7_segment_decoder_3: pin names not known
  Button button_2 (.out(button_2_out));
  _7_Segment_Display u_7_segment_display_4 ();  // open: g, f, a, b, e, d, c, dp
  // _7_Segment_Display 7_segment_display_5: pin names not known; wires that end beside it: viewer_1_s6, viewer_1_s10
  // BCD_to_7_Segment_decoder bcd_to_7_segment_decoder_4: pin names not known
  // BCD_to_7_Segment_decoder bcd_to_7_segment_decoder_5: pin names not known
  _7_Segment_Display u_7_segment_display_6 ();  // open: g, f, a, b, e, d, c, dp
  // BCD_to_7_Segment_decoder bcd_to_7_segment_decoder_6: pin names not known
  R0C0Han r0c0han_1 (
    .E(R0C0), .O0(r0c0han_1_o0), .O1(r0c0han_1_o1), .O2(r0c0han_1_o2), .O3(r0c0han_1_o3), .O4(r0c0han_1_o4),
    .O5(r0c0han_1_o5), .O6(r0c0han_1_o6), .O7(r0c0han_1_o7));
  R1C0Yu r1c0yu_1 (
    .E(R1C0), .O0(r1c0yu_1_o0), .O1(r1c0yu_1_o1), .O2(r1c0yu_1_o2), .O3(r1c0yu_1_o3), .O4(r1c0yu_1_o4),
    .O5(r1c0yu_1_o5), .O6(r1c0yu_1_o6), .O7(r1c0yu_1_o7));
  R2C0A r2c0a_1 (
    .E(R2C0), .O0(r2c0a_1_o0), .O1(r2c0a_1_o1), .O2(r2c0a_1_o2), .O3(r2c0a_1_o3), .O4(r2c0a_1_o4),
    .O5(r2c0a_1_o5), .O6(r2c0a_1_o6), .O7(r2c0a_1_o7));
  R3C0Ja r3c0ja_1 (
    .E(R3C0), .O0(r3c0ja_1_o0), .O1(r3c0ja_1_o1), .O2(r3c0ja_1_o2), .O3(r3c0ja_1_o3), .O4(r3c0ja_1_o4),
    .O5(r3c0ja_1_o5), .O6(r3c0ja_1_o6), .O7(r3c0ja_1_o7));
  R4C0Jeong r4c0jeong_1 (
    .E(R4C0), .O0(r4c0jeong_1_o0), .O1(r4c0jeong_1_o1), .O2(r4c0jeong_1_o2), .O3(r4c0jeong_1_o3),
    .O4(r4c0jeong_1_o4), .O5(r4c0jeong_1_o5), .O6(r4c0jeong_1_o6), .O7(r4c0jeong_1_o7));
  R5C0O r5c0o_1 (
    .E(R5C0), .O0(r5c0o_1_o0), .O1(r5c0o_1_o1), .O2(r5c0o_1_o2), .O3(r5c0o_1_o3), .O4(r5c0o_1_o4),
    .O5(r5c0o_1_o5), .O6(r5c0o_1_o6), .O7(r5c0o_1_o7));
  DotMatrix #(.dotshape("circle"), .matrixcols(8), .matrixrows(8)) dotmatrix_1 (
    .col0(r0c0han_1_o0), .col1(r0c0han_1_o1), .col2(r0c0han_1_o2), .col3(r0c0han_1_o3), .col4(r0c0han_1_o4),
    .col5(r0c0han_1_o5), .col6(r0c0han_1_o6), .col7(r0c0han_1_o7));
  DotMatrix #(.dotshape("circle"), .matrixcols(8), .matrixrows(8)) dotmatrix_2 (
    .col0(r1c0yu_1_o0), .col1(r1c0yu_1_o1), .col2(r1c0yu_1_o2), .col3(r1c0yu_1_o3), .col4(r1c0yu_1_o4),
    .col5(r1c0yu_1_o5), .col6(r1c0yu_1_o6), .col7(r1c0yu_1_o7));
  DotMatrix #(.dotshape("circle"), .matrixcols(8), .matrixrows(8)) dotmatrix_3 (
    .col0(r2c0a_1_o0), .col1(r2c0a_1_o1), .col2(r2c0a_1_o2), .col3(r2c0a_1_o3), .col4(r2c0a_1_o4),
    .col5(r2c0a_1_o5), .col6(r2c0a_1_o6), .col7(r2c0a_1_o7));
  DotMatrix #(.dotshape("circle"), .matrixcols(8), .matrixrows(8)) dotmatrix_4 (
    .col0(r3c0ja_1_o0), .col1(r3c0ja_1_o1), .col2(r3c0ja_1_o2), .col3(r3c0ja_1_o3), .col4(r3c0ja_1_o4),
    .col5(r3c0ja_1_o5), .col6(r3c0ja_1_o6), .col7(r3c0ja_1_o7));
  DotMatrix #(.dotshape("circle"), .matrixcols(8), .matrixrows(8)) dotmatrix_5 (
    .col0(r4c0jeong_1_o0), .col1(r4c0jeong_1_o1), .col2(r4c0jeong_1_o2), .col3(r4c0jeong_1_o3),
    .col4(r4c0jeong_1_o4), .col5(r4c0jeong_1_o5), .col6(r4c0jeong_1_o6), .col7(r4c0jeong_1_o7));
  DotMatrix #(.dotshape("circle"), .matrixcols(8), .matrixrows(8)) dotmatrix_6 (
    .col0(r5c0o_1_o0), .col1(r5c0o_1_o1), .col2(r5c0o_1_o2), .col3(r5c0o_1_o3), .col4(r5c0o_1_o4),
    .col5(r5c0o_1_o5), .col6(r5c0o_1_o6), .col7(r5c0o_1_o7));
  DotMatrix #(.dotshape("circle"), .matrixcols(8), .matrixrows(8)) dotmatrix_7 (
    .col0(r0c1doo_1_o0), .col1(r0c1doo_1_o1), .col2(r0c1doo_1_o2), .col3(r0c1doo_1_o3), .col4(r0c1doo_1_o4),
    .col5(r0c1doo_1_o5), .col6(r0c1doo_1_o6), .col7(r0c1doo_1_o7));
  R0C1Doo r0c1doo_1 (
    .E(R0C1), .O0(r0c1doo_1_o0), .O1(r0c1doo_1_o1), .O2(r0c1doo_1_o2), .O3(r0c1doo_1_o3), .O4(r0c1doo_1_o4),
    .O5(r0c1doo_1_o5), .O6(r0c1doo_1_o6), .O7(r0c1doo_1_o7));
  DotMatrix #(.dotshape("circle"), .matrixcols(8), .matrixrows(8)) dotmatrix_8 (
    .col0(r1c1seoc_1_o0), .col1(r1c1seoc_1_o1), .col2(r1c1seoc_1_o2), .col3(r1c1seoc_1_o3),
    .col4(r1c1seoc_1_o4), .col5(r1c1seoc_1_o5), .col6(r1c1seoc_1_o6), .col7(r1c1seoc_1_o7));
  R1C1Seoc r1c1seoc_1 (
    .E(R1C1), .O0(r1c1seoc_1_o0), .O1(r1c1seoc_1_o1), .O2(r1c1seoc_1_o2), .O3(r1c1seoc_1_o3),
    .O4(r1c1seoc_1_o4), .O5(r1c1seoc_1_o5), .O6(r1c1seoc_1_o6), .O7(r1c1seoc_1_o7));
  DotMatrix #(.dotshape("circle"), .matrixcols(8), .matrixrows(8)) dotmatrix_9 (
    .col0(r2c1hop_1_o0), .col1(r2c1hop_1_o1), .col2(r2c1hop_1_o2), .col3(r2c1hop_1_o3), .col4(r2c1hop_1_o4),
    .col5(r2c1hop_1_o5), .col6(r2c1hop_1_o6), .col7(r2c1hop_1_o7));
  R2C1Hop r2c1hop_1 (
    .E(R2C1), .O0(r2c1hop_1_o0), .O1(r2c1hop_1_o1), .O2(r2c1hop_1_o2), .O3(r2c1hop_1_o3), .O4(r2c1hop_1_o4),
    .O5(r2c1hop_1_o5), .O6(r2c1hop_1_o6), .O7(r2c1hop_1_o7));
  DotMatrix #(.dotshape("circle"), .matrixcols(8), .matrixrows(8)) dotmatrix_10 (
    .col0(r3c1yi_1_o0), .col1(r3c1yi_1_o1), .col2(r3c1yi_1_o2), .col3(r3c1yi_1_o3), .col4(r3c1yi_1_o4),
    .col5(r3c1yi_1_o5), .col6(r3c1yi_1_o6), .col7(r3c1yi_1_o7));
  R3C1Yi r3c1yi_1 (
    .E(R3C1), .O0(r3c1yi_1_o0), .O1(r3c1yi_1_o1), .O2(r3c1yi_1_o2), .O3(r3c1yi_1_o3), .O4(r3c1yi_1_o4),
    .O5(r3c1yi_1_o5), .O6(r3c1yi_1_o6), .O7(r3c1yi_1_o7));
  DotMatrix #(.dotshape("circle"), .matrixcols(8), .matrixrows(8)) dotmatrix_11 (
    .col0(r4c1il_1_o0), .col1(r4c1il_1_o1), .col2(r4c1il_1_o2), .col3(r4c1il_1_o3), .col4(r4c1il_1_o4),
    .col5(r4c1il_1_o5), .col6(r4c1il_1_o6), .col7(r4c1il_1_o7));
  R4C1Il r4c1il_1 (
    .E(R4C1), .O0(r4c1il_1_o0), .O1(r4c1il_1_o1), .O2(r4c1il_1_o2), .O3(r4c1il_1_o3), .O4(r4c1il_1_o4),
    .O5(r4c1il_1_o5), .O6(r4c1il_1_o6), .O7(r4c1il_1_o7));
  DotMatrix #(.dotshape("circle"), .matrixcols(8), .matrixrows(8)) dotmatrix_12 (
    .col0(r5c1o_1_o0), .col1(r5c1o_1_o1), .col2(r5c1o_1_o2), .col3(r5c1o_1_o3), .col4(r5c1o_1_o4),
    .col5(r5c1o_1_o5), .col6(r5c1o_1_o6), .col7(r5c1o_1_o7));
  R5C1O r5c1o_1 (
    .E(R5C1), .O0(r5c1o_1_o0), .O1(r5c1o_1_o1), .O2(r5c1o_1_o2), .O3(r5c1o_1_o3), .O4(r5c1o_1_o4),
    .O5(r5c1o_1_o5), .O6(r5c1o_1_o6), .O7(r5c1o_1_o7));
  DotMatrix #(.dotshape("circle"), .matrixcols(8), .matrixrows(8)) dotmatrix_13 (
    .col0(r0c2se_1_o0), .col1(r0c2se_1_o1), .col2(r0c2se_1_o2), .col3(r0c2se_1_o3), .col4(r0c2se_1_o4),
    .col5(r0c2se_1_o5), .col6(r0c2se_1_o6), .col7(r0c2se_1_o7));
  R0C2Se r0c2se_1 (
    .E(R0C2), .O0(r0c2se_1_o0), .O1(r0c2se_1_o1), .O2(r0c2se_1_o2), .O3(r0c2se_1_o3), .O4(r0c2se_1_o4),
    .O5(r0c2se_1_o5), .O6(r0c2se_1_o6), .O7(r0c2se_1_o7));
  DotMatrix #(.dotshape("circle"), .matrixcols(8), .matrixrows(8)) dotmatrix_14 (
    .col0(r1c2il_1_o0), .col1(r1c2il_1_o1), .col2(r1c2il_1_o2), .col3(r1c2il_1_o3), .col4(r1c2il_1_o4),
    .col5(r1c2il_1_o5), .col6(r1c2il_1_o6), .col7(r1c2il_1_o7));
  R1C2Il r1c2il_1 (
    .E(R1C2), .O0(r1c2il_1_o0), .O1(r1c2il_1_o1), .O2(r1c2il_1_o2), .O3(r1c2il_1_o3), .O4(r1c2il_1_o4),
    .O5(r1c2il_1_o5), .O6(r1c2il_1_o6), .O7(r1c2il_1_o7));
  DotMatrix #(.dotshape("circle"), .matrixcols(8), .matrixrows(8)) dotmatrix_15 (
    .col0(r2c2yul_1_o0), .col1(r2c2yul_1_o1), .col2(r2c2yul_1_o2), .col3(r2c2yul_1_o3), .col4(r2c2yul_1_o4),
    .col5(r2c2yul_1_o5), .col6(r2c2yul_1_o6), .col7(r2c2yul_1_o7));
  R2C2Yul r2c2yul_1 (
    .E(R2C2), .O0(r2c2yul_1_o0), .O1(r2c2yul_1_o1), .O2(r2c2yul_1_o2), .O3(r2c2yul_1_o3), .O4(r2c2yul_1_o4),
    .O5(r2c2yul_1_o5), .O6(r2c2yul_1_o6), .O7(r2c2yul_1_o7));
  DotMatrix #(.dotshape("circle"), .matrixcols(8), .matrixrows(8)) dotmatrix_16 (
    .col0(r3c2sam_1_o0), .col1(r3c2sam_1_o1), .col2(r3c2sam_1_o2), .col3(r3c2sam_1_o3), .col4(r3c2sam_1_o4),
    .col5(r3c2sam_1_o5), .col6(r3c2sam_1_o6), .col7(r3c2sam_1_o7));
  R3C2Sam r3c2sam_1 (
    .E(R3C2), .O0(r3c2sam_1_o0), .O1(r3c2sam_1_o1), .O2(r3c2sam_1_o2), .O3(r3c2sam_1_o3), .O4(r3c2sam_1_o4),
    .O5(r3c2sam_1_o5), .O6(r3c2sam_1_o6), .O7(r3c2sam_1_o7));
  DotMatrix #(.dotshape("circle"), .matrixcols(8), .matrixrows(8)) dotmatrix_17 (
    .col0(r4c2yi_1_o0), .col1(r4c2yi_1_o1), .col2(r4c2yi_1_o2), .col3(r4c2yi_1_o3), .col4(r4c2yi_1_o4),
    .col5(r4c2yi_1_o5), .col6(r4c2yi_1_o6), .col7(r4c2yi_1_o7));
  R4C2Yi r4c2yi_1 (
    .E(R4C2), .O0(r4c2yi_1_o0), .O1(r4c2yi_1_o1), .O2(r4c2yi_1_o2), .O3(r4c2yi_1_o3), .O4(r4c2yi_1_o4),
    .O5(r4c2yi_1_o5), .O6(r4c2yi_1_o6), .O7(r4c2yi_1_o7));
  DotMatrix #(.dotshape("circle"), .matrixcols(8), .matrixrows(8)) dotmatrix_18 (
    .col0(r5c2chil_1_o0), .col1(r5c2chil_1_o1), .col2(r5c2chil_1_o2), .col3(r5c2chil_1_o3),
    .col4(r5c2chil_1_o4), .col5(r5c2chil_1_o5), .col6(r5c2chil_1_o6), .col7(r5c2chil_1_o7));
  R5C2Chil r5c2chil_1 (
    .E(R5C2), .O0(r5c2chil_1_o0), .O1(r5c2chil_1_o1), .O2(r5c2chil_1_o2), .O3(r5c2chil_1_o3),
    .O4(r5c2chil_1_o4), .O5(r5c2chil_1_o5), .O6(r5c2chil_1_o6), .O7(r5c2chil_1_o7));
  R0C3Ne r0c3ne_1 (
    .E(R0C3), .O0(r0c3ne_1_o0), .O1(r0c3ne_1_o1), .O2(r0c3ne_1_o2), .O3(r0c3ne_1_o3), .O4(r0c3ne_1_o4),
    .O5(r0c3ne_1_o5), .O6(r0c3ne_1_o6), .O7(r0c3ne_1_o7));
  R1C3Goq r1c3goq_1 (
    .E(R1C3), .O0(r1c3goq_1_o0), .O1(r1c3goq_1_o1), .O2(r1c3goq_1_o2), .O3(r1c3goq_1_o3), .O4(r1c3goq_1_o4),
    .O5(r1c3goq_1_o5), .O6(r1c3goq_1_o6), .O7(r1c3goq_1_o7));
  R2C3Han r2c3han_1 (
    .E(R2C3), .O0(r2c3han_1_o0), .O1(r2c3han_1_o1), .O2(r2c3han_1_o2), .O3(r2c3han_1_o3), .O4(r2c3han_1_o4),
    .O5(r2c3han_1_o5), .O6(r2c3han_1_o6), .O7(r2c3han_1_o7));
  R3C3Sa r3c3sa_1 (
    .E(R3C3), .O0(r3c3sa_1_o0), .O1(r3c3sa_1_o1), .O2(r3c3sa_1_o2), .O3(r3c3sa_1_o3), .O4(r3c3sa_1_o4),
    .O5(r3c3sa_1_o5), .O6(r3c3sa_1_o6), .O7(r3c3sa_1_o7));
  R4C3Sam r4c3sam_1 (
    .E(R4C3), .O0(r4c3sam_1_o0), .O1(r4c3sam_1_o1), .O2(r4c3sam_1_o2), .O3(r4c3sam_1_o3), .O4(r4c3sam_1_o4),
    .O5(r4c3sam_1_o5), .O6(r4c3sam_1_o6), .O7(r4c3sam_1_o7));
  R5C3Pal r5c3pal_1 (
    .E(R5C3), .O0(r5c3pal_1_o0), .O1(r5c3pal_1_o1), .O2(r5c3pal_1_o2), .O3(r5c3pal_1_o3), .O4(r5c3pal_1_o4),
    .O5(r5c3pal_1_o5), .O6(r5c3pal_1_o6), .O7(r5c3pal_1_o7));
  DotMatrix #(.dotshape("circle"), .matrixcols(8), .matrixrows(8)) dotmatrix_19 (
    .col0(r0c3ne_1_o0), .col1(r0c3ne_1_o1), .col2(r0c3ne_1_o2), .col3(r0c3ne_1_o3), .col4(r0c3ne_1_o4),
    .col5(r0c3ne_1_o5), .col6(r0c3ne_1_o6), .col7(r0c3ne_1_o7));
  DotMatrix #(.dotshape("circle"), .matrixcols(8), .matrixrows(8)) dotmatrix_20 (
    .col0(r1c3goq_1_o0), .col1(r1c3goq_1_o1), .col2(r1c3goq_1_o2), .col3(r1c3goq_1_o3), .col4(r1c3goq_1_o4),
    .col5(r1c3goq_1_o5), .col6(r1c3goq_1_o6), .col7(r1c3goq_1_o7));
  DotMatrix #(.dotshape("circle"), .matrixcols(8), .matrixrows(8)) dotmatrix_21 (
    .col0(r2c3han_1_o0), .col1(r2c3han_1_o1), .col2(r2c3han_1_o2), .col3(r2c3han_1_o3), .col4(r2c3han_1_o4),
    .col5(r2c3han_1_o5), .col6(r2c3han_1_o6), .col7(r2c3han_1_o7));
  DotMatrix #(.dotshape("circle"), .matrixcols(8), .matrixrows(8)) dotmatrix_22 (
    .col0(r3c3sa_1_o0), .col1(r3c3sa_1_o1), .col2(r3c3sa_1_o2), .col3(r3c3sa_1_o3), .col4(r3c3sa_1_o4),
    .col5(r3c3sa_1_o5), .col6(r3c3sa_1_o6), .col7(r3c3sa_1_o7));
  DotMatrix #(.dotshape("circle"), .matrixcols(8), .matrixrows(8)) dotmatrix_23 (
    .col0(r4c3sam_1_o0), .col1(r4c3sam_1_o1), .col2(r4c3sam_1_o2), .col3(r4c3sam_1_o3), .col4(r4c3sam_1_o4),
    .col5(r4c3sam_1_o5), .col6(r4c3sam_1_o6), .col7(r4c3sam_1_o7));
  DotMatrix #(.dotshape("circle"), .matrixcols(8), .matrixrows(8)) dotmatrix_24 (
    .col0(r5c3pal_1_o0), .col1(r5c3pal_1_o1), .col2(r5c3pal_1_o2), .col3(r5c3pal_1_o3), .col4(r5c3pal_1_o4),
    .col5(r5c3pal_1_o5), .col6(r5c3pal_1_o6), .col7(r5c3pal_1_o7));
  R0C4Da r0c4da_1 (
    .E(R0C4), .O0(r0c4da_1_o0), .O1(r0c4da_1_o1), .O2(r0c4da_1_o2), .O3(r0c4da_1_o3), .O4(r0c4da_1_o4),
    .O5(r0c4da_1_o5), .O6(r0c4da_1_o6), .O7(r0c4da_1_o7));
  R1C4Yu r1c4yu_1 (
    .E(R1C4), .O0(r1c4yu_1_o0), .O1(r1c4yu_1_o1), .O2(r1c4yu_1_o2), .O3(r1c4yu_1_o3), .O4(r1c4yu_1_o4),
    .O5(r1c4yu_1_o5), .O6(r1c4yu_1_o6), .O7(r1c4yu_1_o7));
  R2C4Doo r2c4doo_1 (
    .E(R2C4), .O0(r2c4doo_1_o0), .O1(r2c4doo_1_o1), .O2(r2c4doo_1_o2), .O3(r2c4doo_1_o3), .O4(r2c4doo_1_o4),
    .O5(r2c4doo_1_o5), .O6(r2c4doo_1_o6), .O7(r2c4doo_1_o7));
  R3C4O r3c4o_1 (
    .E(R3C4), .O0(r3c4o_1_o0), .O1(r3c4o_1_o1), .O2(r3c4o_1_o2), .O3(r3c4o_1_o3), .O4(r3c4o_1_o4),
    .O5(r3c4o_1_o5), .O6(r3c4o_1_o6), .O7(r3c4o_1_o7));
  R4C4Sa r4c4sa_1 (
    .E(R4C4), .O0(r4c4sa_1_o0), .O1(r4c4sa_1_o1), .O2(r4c4sa_1_o2), .O3(r4c4sa_1_o3), .O4(r4c4sa_1_o4),
    .O5(r4c4sa_1_o5), .O6(r4c4sa_1_o6), .O7(r4c4sa_1_o7));
  R5C4Koo r5c4koo_1 (
    .E(R5C4), .O0(r5c4koo_1_o0), .O1(r5c4koo_1_o1), .O2(r5c4koo_1_o2), .O3(r5c4koo_1_o3), .O4(r5c4koo_1_o4),
    .O5(r5c4koo_1_o5), .O6(r5c4koo_1_o6), .O7(r5c4koo_1_o7));
  DotMatrix #(.dotshape("circle"), .matrixcols(8), .matrixrows(8)) dotmatrix_25 (
    .col0(r0c4da_1_o0), .col1(r0c4da_1_o1), .col2(r0c4da_1_o2), .col3(r0c4da_1_o3), .col4(r0c4da_1_o4),
    .col5(r0c4da_1_o5), .col6(r0c4da_1_o6), .col7(r0c4da_1_o7));
  DotMatrix #(.dotshape("circle"), .matrixcols(8), .matrixrows(8)) dotmatrix_26 (
    .col0(r1c4yu_1_o0), .col1(r1c4yu_1_o1), .col2(r1c4yu_1_o2), .col3(r1c4yu_1_o3), .col4(r1c4yu_1_o4),
    .col5(r1c4yu_1_o5), .col6(r1c4yu_1_o6), .col7(r1c4yu_1_o7));
  DotMatrix #(.dotshape("circle"), .matrixcols(8), .matrixrows(8)) dotmatrix_27 (
    .col0(r2c4doo_1_o0), .col1(r2c4doo_1_o1), .col2(r2c4doo_1_o2), .col3(r2c4doo_1_o3), .col4(r2c4doo_1_o4),
    .col5(r2c4doo_1_o5), .col6(r2c4doo_1_o6), .col7(r2c4doo_1_o7));
  DotMatrix #(.dotshape("circle"), .matrixcols(8), .matrixrows(8)) dotmatrix_28 (
    .col0(r3c4o_1_o0), .col1(r3c4o_1_o1), .col2(r3c4o_1_o2), .col3(r3c4o_1_o3), .col4(r3c4o_1_o4),
    .col5(r3c4o_1_o5), .col6(r3c4o_1_o6), .col7(r3c4o_1_o7));
  DotMatrix #(.dotshape("circle"), .matrixcols(8), .matrixrows(8)) dotmatrix_29 (
    .col0(r4c4sa_1_o0), .col1(r4c4sa_1_o1), .col2(r4c4sa_1_o2), .col3(r4c4sa_1_o3), .col4(r4c4sa_1_o4),
    .col5(r4c4sa_1_o5), .col6(r4c4sa_1_o6), .col7(r4c4sa_1_o7));
  DotMatrix #(.dotshape("circle"), .matrixcols(8), .matrixrows(8)) dotmatrix_30 (
    .col0(r5c4koo_1_o0), .col1(r5c4koo_1_o1), .col2(r5c4koo_1_o2), .col3(r5c4koo_1_o3), .col4(r5c4koo_1_o4),
    .col5(r5c4koo_1_o5), .col6(r5c4koo_1_o6), .col7(r5c4koo_1_o7));
  DotMatrix #(.dotshape("circle"), .matrixcols(8), .matrixrows(8)) dotmatrix_31 (
    .col0(r0c5seoc_1_o0), .col1(r0c5seoc_1_o1), .col2(r0c5seoc_1_o2), .col3(r0c5seoc_1_o3),
    .col4(r0c5seoc_1_o4), .col5(r0c5seoc_1_o5), .col6(r0c5seoc_1_o6), .col7(r0c5seoc_1_o7));
  R0C5Seoc r0c5seoc_1 (
    .E(R0C5), .O0(r0c5seoc_1_o0), .O1(r0c5seoc_1_o1), .O2(r0c5seoc_1_o2), .O3(r0c5seoc_1_o3),
    .O4(r0c5seoc_1_o4), .O5(r0c5seoc_1_o5), .O6(r0c5seoc_1_o6), .O7(r0c5seoc_1_o7));
  DotMatrix #(.dotshape("circle"), .matrixcols(8), .matrixrows(8)) dotmatrix_32 (
    .col0(r1c5durb_1_o0), .col1(r1c5durb_1_o1), .col2(r1c5durb_1_o2), .col3(r1c5durb_1_o3),
    .col4(r1c5durb_1_o4), .col5(r1c5durb_1_o5), .col6(r1c5durb_1_o6), .col7(r1c5durb_1_o7));
  R1C5Durb r1c5durb_1 (
    .E(R1C5), .O0(r1c5durb_1_o0), .O1(r1c5durb_1_o1), .O2(r1c5durb_1_o2), .O3(r1c5durb_1_o3),
    .O4(r1c5durb_1_o4), .O5(r1c5durb_1_o5), .O6(r1c5durb_1_o6), .O7(r1c5durb_1_o7));
  DotMatrix #(.dotshape("circle"), .matrixcols(8), .matrixrows(8)) dotmatrix_33 (
    .col0(r2c5si_1_o0), .col1(r2c5si_1_o1), .col2(r2c5si_1_o2), .col3(r2c5si_1_o3), .col4(r2c5si_1_o4),
    .col5(r2c5si_1_o5), .col6(r2c5si_1_o6), .col7(r2c5si_1_o7));
  R2C5Si r2c5si_1 (
    .E(R2C5), .O0(r2c5si_1_o0), .O1(r2c5si_1_o1), .O2(r2c5si_1_o2), .O3(r2c5si_1_o3), .O4(r2c5si_1_o4),
    .O5(r2c5si_1_o5), .O6(r2c5si_1_o6), .O7(r2c5si_1_o7));
  DotMatrix #(.dotshape("circle"), .matrixcols(8), .matrixrows(8)) dotmatrix_34 (
    .col0(r3c5siq_1_o0), .col1(r3c5siq_1_o1), .col2(r3c5siq_1_o2), .col3(r3c5siq_1_o3), .col4(r3c5siq_1_o4),
    .col5(r3c5siq_1_o5), .col6(r3c5siq_1_o6), .col7(r3c5siq_1_o7));
  R3C5Siq r3c5siq_1 (
    .E(R3C5), .O0(r3c5siq_1_o0), .O1(r3c5siq_1_o1), .O2(r3c5siq_1_o2), .O3(r3c5siq_1_o3), .O4(r3c5siq_1_o4),
    .O5(r3c5siq_1_o5), .O6(r3c5siq_1_o6), .O7(r3c5siq_1_o7));
  DotMatrix #(.dotshape("circle"), .matrixcols(8), .matrixrows(8)) dotmatrix_35 (
    .col0(r4c5yuk_1_o0), .col1(r4c5yuk_1_o1), .col2(r4c5yuk_1_o2), .col3(r4c5yuk_1_o3), .col4(r4c5yuk_1_o4),
    .col5(r4c5yuk_1_o5), .col6(r4c5yuk_1_o6), .col7(r4c5yuk_1_o7));
  R4C5Yuk r4c5yuk_1 (
    .E(R4C5), .O0(r4c5yuk_1_o0), .O1(r4c5yuk_1_o1), .O2(r4c5yuk_1_o2), .O3(r4c5yuk_1_o3), .O4(r4c5yuk_1_o4),
    .O5(r4c5yuk_1_o5), .O6(r4c5yuk_1_o6), .O7(r4c5yuk_1_o7));
  DotMatrix #(.dotshape("circle"), .matrixcols(8), .matrixrows(8)) dotmatrix_36 (
    .col0(r5c5boon_1_o0), .col1(r5c5boon_1_o1), .col2(r5c5boon_1_o2), .col3(r5c5boon_1_o3),
    .col4(r5c5boon_1_o4), .col5(r5c5boon_1_o5), .col6(r5c5boon_1_o6), .col7(r5c5boon_1_o7));
  R5C5Boon r5c5boon_1 (
    .E(R5C5), .O0(r5c5boon_1_o0), .O1(r5c5boon_1_o1), .O2(r5c5boon_1_o2), .O3(r5c5boon_1_o3),
    .O4(r5c5boon_1_o4), .O5(r5c5boon_1_o5), .O6(r5c5boon_1_o6), .O7(r5c5boon_1_o7));

  // Notes on the sheet:
  //   Mode: 0=time set, 1=run
  //   시
  //   18101269 정동하
  //   분
  //   초
  //   1. Mode를 1로 설정해주세요.
  //   2. logisim 상단 Simulate 에서 
endmodule
